// Logisim project 2.circ as structural Verilog: 1 circuit, main circuit main
module main (
  output out_1
);

  wire A, A_B_out, B, C, CD_out, clock_1_out, D, go, nC_nD___CD_out, nC_nD_out, not_1_out, not_2_out,
       Reset_out, t_ff_1_q, t_ff_2_q, t_ff_3_q, t_ff_4_q;

  // Probe on {A, B, C, D}
  Clock clock_1 (.out(clock_1_out));
  // Probe on out_1
  T_Flip_Flop t_ff_1 (.clk(clock_1_out), .T(1'b1), .Q(t_ff_1_q), .Qn(D), .preset(Reset_out), .en(go));  // open: reset
  T_Flip_Flop t_ff_2 (.clk(t_ff_1_q), .T(1'b1), .Q(t_ff_2_q), .Qn(C), .preset(Reset_out));  // open: reset, en
  TTY #(.rows(1), .cols(18)) tty_1 (.data({6'b011000, out_1}), .clk(clock_1_out), .we(go), .clr(Reset_out));
  T_Flip_Flop t_ff_3 (.clk(t_ff_4_q), .T(1'b1), .Q(t_ff_3_q), .Qn(A), .preset(Reset_out));  // open: reset, en
  T_Flip_Flop t_ff_4 (.clk(t_ff_2_q), .T(1'b1), .Q(t_ff_4_q), .Qn(B), .preset(Reset_out));  // open: reset, en
  T_Flip_Flop t_ff_5 (.clk(t_ff_3_q), .T(1'b1), .Q(go), .preset(Reset_out));  // open: Qn, reset, en
  Button Reset (.out(Reset_out));
  not not_1 (not_1_out, C);
  not not_2 (not_2_out, D);
  and nC_nD (nC_nD_out, not_1_out, not_2_out);
  and CD (CD_out, C, D);
  or A_B (A_B_out, A, B);
  or nC_nD___CD (nC_nD___CD_out, nC_nD_out, CD_out);
  and and_1 (out_1, A_B_out, nC_nD___CD_out);

  // Other names for the same wires on the sheet: f = out_1

  // Notes on the sheet:
  //   000010011001d00d
endmodule
