// Logisim project 3.circ as structural Verilog: 1 circuit, main circuit main
module main (
  input  [5:0] in_1,
  output [1:0] out_2,
  output [2:0] out_3,
  output [1:0] out_4,
  output [2:0] out_5
);

  wire A, B, C, clock_1_out, D, E, F, go, Reset_out, t_ff_1_q, t_ff_2_q, t_ff_3_q, t_ff_4_q, t_ff_5_q,
       t_ff_6_q, X0, X1, X2;
  wire [3:0] bit_extender_1_out;

  // Probe on {A, B, C, D, E, F}
  // Probe on {X2, X1, X0}
  Clock clock_1 (.out(clock_1_out));
  TTY #(.rows(1), .cols(65)) tty_1 (.data({4'b0110, X2, X1, X0}), .clk(clock_1_out), .we(go), .clr(Reset_out));
  T_Flip_Flop t_ff_1 (.clk(clock_1_out), .T(1'b1), .Q(t_ff_1_q), .Qn(F), .preset(Reset_out), .en(go));  // open: reset
  T_Flip_Flop t_ff_2 (.clk(t_ff_1_q), .T(1'b1), .Q(t_ff_2_q), .Qn(E), .preset(Reset_out));  // open: reset, en
  BitAdder #(.width(1)) bitadder_1 (.in0(F), .in1(E), .in2(D), .in3(C), .in4(B), .in5(A), .out({X2, X1, X0}));
  BitAdder #(.width(1)) bitadder_2 (.in0(in_1[5]), .in1(in_1[4]), .out(out_2));
  BitAdder #(.width(1)) bitadder_3 (.in0(in_1[3]), .in1(in_1[2]), .out(out_4));
  BitAdder #(.width(1)) bitadder_4 (
    .in0(in_1[0]), .in1(in_1[1]), .in2(in_1[2]), .in3(in_1[3]), .in4(in_1[4]), .in5(in_1[5]), .out(out_5));
  T_Flip_Flop t_ff_3 (.clk(t_ff_2_q), .T(1'b1), .Q(t_ff_3_q), .Qn(D), .preset(Reset_out));  // open: reset, en
  BitAdder #(.width(1)) bitadder_5 (.in0(in_1[1]), .in1(in_1[0]));  // open: out
  T_Flip_Flop t_ff_4 (.clk(t_ff_3_q), .T(1'b1), .Q(t_ff_4_q), .Qn(C), .preset(Reset_out));  // open: reset, en
  BitAdder #(.width(2)) bitadder_6 (.in0(out_2), .in1(out_4), .out(out_3));
  T_Flip_Flop t_ff_5 (.clk(t_ff_4_q), .T(1'b1), .Q(t_ff_5_q), .Qn(B), .preset(Reset_out));  // open: reset, en
  assign bit_extender_1_out = {{1{1'b0}}, out_3};  // Bit_Extender bit_extender_1
  T_Flip_Flop t_ff_6 (.clk(t_ff_5_q), .T(1'b1), .Q(t_ff_6_q), .Qn(A), .preset(Reset_out));  // open: reset, en
  T_Flip_Flop t_ff_7 (.clk(t_ff_6_q), .T(1'b1), .Q(go), .preset(Reset_out));  // open: Qn, reset, en
  Hex_Digit_Display hex_digit_display_1 (.value(bit_extender_1_out));  // open: dp
  Button Reset (.out(Reset_out));

  // Notes on the sheet:
  //   Early iteration of the circuit, before I knew it was possible to increase the inputs to the bit adder.
  //   0112122312232334122323342334344512232334233434452334344534454556
endmodule
