// Logisim project 5.circ as structural Verilog: 1 circuit, main circuit main
module main (
  input  in_1,
  input  in_2,
  input  in_3,
  input  in_4,
  input  in_5,
  input  in_6,
  input  in_7,
  input  A,
  input  B,
  input  C,
  output out_11,
  output out_12,
  output out_13,
  output out_14,
  output out_15,
  output out_16
);

  wire A_t, and_1_out, and_2_out, and_3_out, and_4_out, and_5_out, and_7_out, and_8_out, B_t, C_t,
       clock_1_out, go, multiplexer_3_out, not_1_out, not_2_out, not_3_out, not_4_out, not_5_out, not_6_out,
       not_7_out, not_8_out, not_9_out, not_10_out, not_11_out, Reset_out, t_ff_1_q, t_ff_2_q, t_ff_3_q;

  // Probe on {A_t, B_t, C_t}
  Clock clock_1 (.out(clock_1_out));
  T_Flip_Flop t_ff_1 (.clk(clock_1_out), .T(1'b1), .Q(t_ff_1_q), .Qn(C_t), .preset(Reset_out), .en(go));  // open: reset
  // Probe on out_11
  T_Flip_Flop t_ff_2 (.clk(t_ff_1_q), .T(1'b1), .Q(t_ff_2_q), .Qn(B_t), .preset(Reset_out));  // open: reset, en
  not not_1 (not_1_out, in_1);
  TTY #(.rows(1), .cols(10)) tty_1 (.data({6'b011000, out_11}), .clk(clock_1_out), .we(go), .clr(Reset_out));
  T_Flip_Flop t_ff_3 (.clk(t_ff_2_q), .T(1'b1), .Q(t_ff_3_q), .Qn(A_t), .preset(Reset_out));  // open: reset, en
  and and_1 (and_1_out, not_1_out, in_3);
  and and_2 (and_2_out, in_1, in_5);
  T_Flip_Flop t_ff_4 (.clk(t_ff_3_q), .T(1'b1), .Q(go), .preset(Reset_out));  // open: Qn, reset, en
  or or_1 (out_13, and_1_out, and_2_out);
  not not_2 (not_2_out, A);
  not not_3 (not_3_out, C);
  not not_4 (not_4_out, C);
  not not_5 (not_5_out, A);
  Button Reset (.out(Reset_out));
  Multiplexer multiplexer_1 (.in0(in_3), .in1(in_5), .out(out_14), .sel(in_1));  // open: en
  and and_3 (and_3_out, not_2_out, not_3_out);
  and and_4 (and_4_out, B, not_4_out);
  and and_5 (and_5_out, not_5_out, B);
  or or_2 (out_16, and_3_out, and_4_out, and_5_out);
  not not_6 (not_6_out, in_7);
  and and_6 (out_12, in_2, in_4);
  Multiplexer multiplexer_2 (.in0(in_6), .in1(in_7), .out(out_15), .sel(not_6_out));  // open: en
  not not_7 (not_7_out, A_t);
  and and_7 (and_7_out, not_7_out, not_8_out);
  not not_8 (not_8_out, C_t);
  and and_8 (and_8_out, B_t, not_9_out);
  not not_9 (not_9_out, C_t);
  not not_10 (not_10_out, A_t);
  Multiplexer multiplexer_3 (.in0(not_10_out), .in1(B_t), .out(multiplexer_3_out), .sel(not_11_out));  // open: en
  not not_11 (not_11_out, B_t);
  or or_3 (out_11, and_7_out, and_8_out, multiplexer_3_out);

  // Other names for the same wires on the sheet: f = out_11

  // Notes on the sheet:
  //   10110010
endmodule
