// Logisim project 6.circ as structural Verilog: 1 circuit, main circuit main
module main (
);

  wire a, and_1_out, and_2_out, and_3_out, and_4_out, and_5_out, and_6_out, b, c, clock_1_out, go, not_1_out,
       not_4_out, not_5_out, or_1_out, Reset_out, t_ff_1_q, t_ff_2_q, t_ff_3_q, w0, w1, w2, w3;

  and and_1 (and_1_out, w0, ~w1, ~w2, ~w3);  // AND_Gate
  and and_2 (and_2_out, ~w0, ~w1, w2, ~w3);  // AND_Gate
  and and_3 (and_3_out, w0, w1, w2, ~w3);  // AND_Gate
  and and_4 (and_4_out, ~w0, ~w1, w2, ~w3);  // AND_Gate
  not not_1 (not_1_out, and_5_out);
  and and_5 (and_5_out, w2, ~w3);  // AND_Gate
  and and_6 (and_6_out, ~w0, w1, ~w2, ~w3);  // AND_Gate
  not not_2 (a, or_1_out);
  or or_1 (or_1_out, and_1_out, and_2_out);
  or or_2 (b, and_3_out, and_4_out, not_1_out);
  not not_3 (c, and_6_out);
  Clock clock_1 (.out(clock_1_out));
  // Probe on {w3, w2, w1, w0}
  T_Flip_Flop t_ff_1 (.clk(clock_1_out), .T(1'b1), .Q(t_ff_1_q), .Qn(w0), .preset(Reset_out), .en(go));  // open: reset
  nand nand_1 (go, not_4_out, w1, not_5_out, w3);
  // Probe on a
  // Probe on b
  // Probe on c
  T_Flip_Flop t_ff_2 (.clk(t_ff_1_q), .T(1'b1), .Q(t_ff_2_q), .Qn(w1), .preset(Reset_out));  // open: reset, en
  not not_4 (not_4_out, w0);
  not not_5 (not_5_out, w2);
  TTY #(.rows(1), .cols(18)) tty_1 (.data({6'b011000, a}), .clk(clock_1_out), .we(go), .clr(Reset_out));
  TTY #(.rows(1), .cols(18)) tty_2 (.data({6'b011000, b}), .clk(clock_1_out), .we(go), .clr(Reset_out));
  TTY #(.rows(1), .cols(18)) tty_3 (.data({6'b011000, c}), .clk(clock_1_out), .we(go), .clr(Reset_out));
  T_Flip_Flop t_ff_3 (.clk(t_ff_2_q), .T(1'b1), .Q(t_ff_3_q), .Qn(w2), .preset(Reset_out));  // open: reset, en
  T_Flip_Flop t_ff_4 (.clk(t_ff_3_q), .T(1'b1), .Qn(w3), .preset(Reset_out));  // open: Q, reset, en
  Button Reset (.out(Reset_out));

  // Notes on the sheet:
  //   1011011111
  //   1111100111
  //   1101111111
  //   go until 10
endmodule
