// Logisim project 7.circ as structural Verilog: 1 circuit, main circuit main
module main (
);

  wire A0, A1, A2, adder_1_out, adder_2_out, adder_3_out, adder_4_out, adder_5_out, adder_6_out, adder_7_out,
       adder_8_out, adder_9_out, adder_10_out, adder_11_out, adder_12_out, adder_13_out, adder_14_out, C0,
       C1, C2, C3, clock_1_out, D0, D1, D2, D3, D4, D5, D6, D7, decoder_1_out1, decoder_1_out2,
       decoder_1_out3, decoder_1_out4, decoder_1_out5, decoder_1_out6, decoder_1_out7, decoder_1_out8,
       decoder_1_out9, decoder_1_out10, decoder_1_out11, decoder_1_out12, decoder_1_out13, decoder_1_out14,
       decoder_1_out15, go, or_1_out, or_2_out, or_4_out, or_10_out, P0, P1, P2, Reset_out, t_ff_1_q,
       t_ff_2_q, t_ff_3_q, t_ff_4_q, t_ff_5_q, t_ff_6_q, Z0, Z1, Z2, Z3, Z4, Z5, Z6, Z7;
  wire [0:0] multiplexer_1_out;
  wire [3:0] xor_1_out;

  Adder #(.width(1)) adder_1 (.a(D0), .b(D1), .out(adder_1_out));  // open: cin, cout
  Adder #(.width(1)) adder_2 (.a(adder_1_out), .b(adder_3_out), .out(adder_2_out));  // open: cin, cout
  Adder #(.width(1)) adder_3 (.a(D3), .b(D4), .out(adder_3_out));  // open: cin, cout
  Adder #(.width(1)) adder_4 (.a(D0), .b(D2), .out(adder_4_out));  // open: cin, cout
  Adder #(.width(1)) adder_5 (.a(adder_4_out), .b(adder_6_out), .out(adder_5_out));  // open: cin, cout
  Adder #(.width(1)) adder_6 (.a(D3), .b(D5), .out(adder_6_out));  // open: cin, cout
  Adder #(.width(1)) adder_7 (.a(D1), .b(D2), .out(adder_7_out));  // open: cin, cout
  Adder #(.width(1)) adder_8 (.a(D3), .b(D7), .out(adder_8_out));  // open: cin, cout
  Adder #(.width(1)) adder_9 (.a(D4), .b(D5), .out(adder_9_out));  // open: cin, cout
  Adder #(.width(1)) adder_10 (.a(D6), .b(D7), .out(adder_10_out));  // open: cin, cout
  Adder #(.width(1)) adder_11 (.a(adder_2_out), .b(D6), .out(adder_11_out));  // open: cin, cout
  Adder #(.width(1)) adder_12 (.a(adder_5_out), .b(D6), .out(adder_12_out));  // open: cin, cout
  Adder #(.width(1)) adder_13 (.a(adder_7_out), .b(adder_8_out), .out(adder_13_out));  // open: cin, cout
  Adder #(.width(1)) adder_14 (.a(adder_9_out), .b(adder_10_out), .out(adder_14_out));  // open: cin, cout
  xor xor_1 (xor_1_out[0], adder_12_out, C1);
  xor xor_2 (xor_1_out[1], adder_13_out, C2);
  xor xor_3 (xor_1_out[2], adder_14_out, C3);
  xor xor_4 (xor_1_out[3], adder_11_out, C0);
  Clock clock_1 (.out(clock_1_out));
  Decoder #(.select(4), .enable("false")) decoder_1 (
    .out1(decoder_1_out1), .out2(decoder_1_out2), .out3(decoder_1_out3), .out4(decoder_1_out4),
    .out5(decoder_1_out5), .out6(decoder_1_out6), .out7(decoder_1_out7), .out8(decoder_1_out8),
    .out9(decoder_1_out9), .out10(decoder_1_out10), .out11(decoder_1_out11), .out12(decoder_1_out12),
    .out13(decoder_1_out13), .out14(decoder_1_out14), .out15(decoder_1_out15), .sel(xor_1_out));  // open: out0
  T_Flip_Flop t_ff_1 (.clk(clock_1_out), .T(1'b1), .Q(t_ff_1_q), .Qn(P0), .preset(Reset_out), .en(go));  // open: reset
  Multiplexer #(.select(3), .disabled(0), .enable("false")) multiplexer_1 (
    .in0(Z7), .in1(Z6), .in2(Z5), .in3(Z4), .in4(Z3), .in5(Z2), .in6(Z1), .in7(Z0),
    .out(multiplexer_1_out[0]), .sel({P2, P1, P0}));
  T_Flip_Flop t_ff_2 (.clk(t_ff_1_q), .T(1'b1), .Q(t_ff_2_q), .Qn(P1), .preset(Reset_out));  // open: reset, en
  TTY #(.cols(8)) tty_1 (.data({6'b011000, multiplexer_1_out[0]}), .clk(clock_1_out), .we(go), .clr(Reset_out));
  T_Flip_Flop t_ff_3 (.clk(t_ff_4_q), .T(1'b1), .Q(t_ff_3_q), .Qn(A0), .preset(Reset_out));  // open: reset, en
  T_Flip_Flop t_ff_4 (.clk(t_ff_2_q), .T(1'b1), .Q(t_ff_4_q), .Qn(P2), .preset(Reset_out));  // open: reset, en
  // Probe on {D7, D6, D5, D4, C3, D3, D2, D1, C2, D0, C1, C0}
  ROM #(.addrWidth(3), .dataWidth(12)) rom_1 (
    .addr({A2, A1, A0}), .data({D7, D6, D5, D4, C3, D3, D2, D1, C2, D0, C1, C0}));  // open: sel
  or or_1 (or_1_out, decoder_1_out1, C0);
  or or_2 (or_2_out, decoder_1_out2, C1);
  T_Flip_Flop t_ff_5 (.clk(t_ff_3_q), .T(1'b1), .Q(t_ff_5_q), .Qn(A1), .preset(Reset_out));  // open: reset, en
  or or_3 (Z0, decoder_1_out3, D0);
  or or_4 (or_4_out, decoder_1_out4, C2);
  or or_5 (Z1, decoder_1_out5, D1);
  or or_6 (Z2, decoder_1_out6, D2);
  or or_7 (Z3, decoder_1_out7, D3);
  or or_8 (Z4, decoder_1_out8, C3);
  or or_9 (Z5, decoder_1_out9, D4);
  or or_10 (or_10_out, decoder_1_out10, D5);
  or or_11 (Z6, decoder_1_out11, D6);
  or or_12 (Z7, decoder_1_out12, D7);
  T_Flip_Flop t_ff_6 (.clk(t_ff_5_q), .T(1'b1), .Q(t_ff_6_q), .Qn(A2), .preset(Reset_out));  // open: reset, en
  T_Flip_Flop t_ff_7 (.clk(t_ff_6_q), .T(1'b1), .Q(go), .preset(Reset_out));  // open: Qn, reset, en
  Button Reset (.out(Reset_out));

  // Notes on the sheet:
  //   Calculated
  //   Recieved
  //   C0
  //   C1
  //   C2
  //   C3
  //   C0
  //   C1
  //   C2
  //   C3
  //   contents of rom_1 (hex, n*v repeats v):
  //   d7 788 a75 a74 275 b75 f75 a77
  //   00101011
  //   01110000
  //   10101111
  //   10101111
  //   10101111
  //   10101111
  //   11111111
  //   10101111
endmodule
