// Logisim project 8bitALU.circ as structural Verilog: 11 circuits, main circuit main
module main (
);

  wire A0, A1, A2, A3, Ad0, Ad1, Ad2, Ad3, B0, B1, B2, B3, C0, C1, C2, C3, C4, CIN, clock_1_out, go,
       Reset_out, S0, S1, t_ff_1_q, t_ff_2_q, t_ff_3_q, t_ff_4_q;
  wire [11:11] rom_1_data;

  Clock clock_1 (.out(clock_1_out));
  T_Flip_Flop t_ff_1 (.clk(clock_1_out), .T(1'b1), .Q(t_ff_1_q), .Qn(Ad0), .preset(Reset_out), .en(go));  // open: reset
  // Probe on {C4, C3, C2, C1, C0}
  T_Flip_Flop t_ff_2 (.clk(t_ff_1_q), .T(1'b1), .Q(t_ff_2_q), .Qn(Ad1), .preset(Reset_out));  // open: reset, en
  // Probe on CIN
  // Probe on {S1, S0}
  TTY #(.rows(1), .cols(16)) tty_1 (.data({2'b10, C4, C3, C2, C1, C0}), .clk(clock_1_out), .we(go), .clr(Reset_out));
  T_Flip_Flop t_ff_3 (.clk(t_ff_2_q), .T(1'b1), .Q(t_ff_3_q), .Qn(Ad2), .preset(Reset_out));  // open: reset, en
  ROM #(.addrWidth(4), .dataWidth(12)) rom_1 (
    .addr({Ad3, Ad2, Ad1, Ad0}), .data({rom_1_data[11], CIN, S1, S0, B3, B2, B1, B0, A3, A2, A1, A0}));  // open: sel
  // Probe on {B3, B2, B1, B0}
  T_Flip_Flop t_ff_4 (.clk(t_ff_3_q), .T(1'b1), .Q(t_ff_4_q), .Qn(Ad3), .preset(Reset_out));  // open: reset, en
  // Probe on {rom_1_data[11], CIN, S1, S0, B3, B2, B1, B0, A3, A2, A1, A0}
  // Probe on {A3, A2, A1, A0}
  Button Reset (.out(Reset_out));
  T_Flip_Flop t_ff_5 (.clk(t_ff_4_q), .T(1'b1), .Q(go), .preset(Reset_out));  // open: Qn, reset, en
  ALU alu_1 ();  // open: B0, B1, B3, B2, A3, A2, A1, A0, B7, B6, B5, B4, A7, A6, A5, A4, D, Cin, Cout, C0, C1, C2, C3, C4, C5, C6, C7, opCode

  // Notes on the sheet:
  //   adds 64 to make printable
  //   contents of rom_1 (hex, n*v repeats v):
  //   0 4ff ac 100 5ff 1ac 200 6ff 2ac 300 7ff 3ac 3c3 73c 37d 7d7
  //   @_X@_^OPS@_VOPTU
endmodule

// s1
module ALU (
  input  A7,
  input  A6,
  input  A5,
  input  A4,
  input  A3,
  input  A2,
  input  A1,
  input  A0,
  input  B7,
  input  B6,
  input  B5,
  input  B4,
  input  B3,
  input  B2,
  input  B1,
  input  B0,
  input  [3:0] opCode,
  input  D,
  input  Cin,
  output C0,
  output C1,
  output C2,
  output C3,
  output C4,
  output C5,
  output C6,
  output C7,
  output Cout
);

  wire [7:0] and_1_out_17, not_1_c0, or_1_out_17, sll_1_out_9, slr_1_out_9, subtraction_1_s0;

  NOT not_1 (
    .A0(A0), .A1(A1), .A2(A2), .A3(A3), .C0(not_1_c0[0]), .C1(not_1_c0[1]), .C2(not_1_c0[2]),
    .C3(not_1_c0[3]), .A4(A4), .A5(A5), .A6(A6), .A7(A7), .C4(not_1_c0[4]), .C5(not_1_c0[5]),
    .C6(not_1_c0[6]), .C7(not_1_c0[7]));
  AND and_1 (
    .A0(A0), .A1(A1), .A2(A2), .A3(A3), .B0(B0), .B1(B1), .B2(B2), .B3(B3), .out_17(and_1_out_17[0]),
    .out_18(and_1_out_17[1]), .out_19(and_1_out_17[2]), .out_20(and_1_out_17[3]), .A4(A4),
    .out_21(and_1_out_17[4]), .B4(B4), .A5(A5), .out_22(and_1_out_17[5]), .B5(B5), .A6(A6),
    .out_23(and_1_out_17[6]), .B6(B6), .A7(A7), .out_24(and_1_out_17[7]), .B7(B7));
  SLR slr_1 (
    .in_1(A0), .in_2(A1), .in_3(A2), .in_4(A3), .in_5(A4), .in_6(A5), .in_7(A6), .in_8(A7),
    .out_9(slr_1_out_9[0]), .out_10(slr_1_out_9[1]), .out_11(slr_1_out_9[2]), .out_12(slr_1_out_9[3]),
    .out_13(slr_1_out_9[4]), .out_14(slr_1_out_9[5]), .out_15(slr_1_out_9[6]), .out_16(slr_1_out_9[7]));
  SLL sll_1 (
    .in_1(A0), .in_2(A1), .in_3(A2), .in_4(A3), .in_5(A4), .in_6(A5), .in_7(A6), .in_8(A7),
    .out_9(sll_1_out_9[0]), .out_10(sll_1_out_9[1]), .out_11(sll_1_out_9[2]), .out_12(sll_1_out_9[3]),
    .out_13(sll_1_out_9[4]), .out_14(sll_1_out_9[5]), .out_15(sll_1_out_9[6]), .out_16(sll_1_out_9[7]));
  OR or_1 (
    .A0(A0), .out_17(or_1_out_17[0]), .B0(B0), .A1(A1), .out_18(or_1_out_17[1]), .B1(B1), .A2(A2),
    .out_19(or_1_out_17[2]), .B2(B2), .A3(A3), .out_20(or_1_out_17[3]), .B3(B3), .A4(A4),
    .out_21(or_1_out_17[4]), .B4(B4), .A5(A5), .out_22(or_1_out_17[5]), .B5(B5), .A6(A6),
    .out_23(or_1_out_17[6]), .B6(B6), .A7(A7), .out_24(or_1_out_17[7]), .B7(B7));
  subtraction subtraction_1 (
    .D(D), .C8(Cout), .S3(subtraction_1_s0[3]), .S2(subtraction_1_s0[2]), .S1(subtraction_1_s0[1]),
    .S0(subtraction_1_s0[0]), .S7(subtraction_1_s0[7]), .S6(subtraction_1_s0[6]), .S5(subtraction_1_s0[5]),
    .S4(subtraction_1_s0[4]), .Cin(Cin), .A5(B5), .B5(A5), .A7(B7), .A6(B6), .B7(A7), .B6(A6), .A0(B0),
    .B0(A0), .A3(B3), .A2(B2), .B3(A3), .B2(A2), .A1(B1), .B1(A1), .A4(B4), .B4(A4));
  Multiplexer #(.select(4), .width(8)) multiplexer_1 (
    .in0(and_1_out_17), .in1(or_1_out_17), .in2(not_1_c0), .in3(subtraction_1_s0),
    .in4({A7, A6, A5, A4, A3, A2, A1, A0}), .in5(sll_1_out_9), .in6(slr_1_out_9),
    .out({C7, C6, C5, C4, C3, C2, C1, C0}), .sel(opCode));  // open: in7, in8, in9, in10, in11, in12, in13, in14, in15, en
endmodule

module AND (
  input  A0,
  input  B0,
  input  A1,
  input  B1,
  input  A2,
  input  B2,
  input  A3,
  input  B3,
  input  A4,
  input  B4,
  input  A5,
  input  B5,
  input  A6,
  input  B6,
  input  A7,
  input  B7,
  output out_17,
  output out_18,
  output out_19,
  output out_20,
  output out_21,
  output out_22,
  output out_23,
  output out_24
);

  and and_1 (out_17, A0, B0);
  and and_2 (out_18, A1, B1);
  and and_3 (out_19, A2, B2);
  and and_4 (out_20, A3, B3);
  and and_5 (out_21, A4, B4);
  and and_6 (out_22, A5, B5);
  and and_7 (out_23, A6, B6);
  and and_8 (out_24, A7, B7);
endmodule

module OR (
  input  A0,
  input  B0,
  input  A1,
  input  B1,
  input  A2,
  input  B2,
  input  A3,
  input  B3,
  input  A4,
  input  B4,
  input  A5,
  input  B5,
  input  A6,
  input  B6,
  input  A7,
  input  B7,
  output out_17,
  output out_18,
  output out_19,
  output out_20,
  output out_21,
  output out_22,
  output out_23,
  output out_24
);

  or or_1 (out_17, A0, B0);
  or or_2 (out_18, A1, B1);
  or or_3 (out_19, A2, B2);
  or or_4 (out_20, A3, B3);
  or or_5 (out_21, A4, B4);
  or or_6 (out_22, A5, B5);
  or or_7 (out_23, A6, B6);
  or or_8 (out_24, A7, B7);
endmodule

module NOT (
  input  A0,
  input  A1,
  input  A2,
  input  A3,
  input  A4,
  input  A5,
  input  A6,
  input  A7,
  output C0,
  output C1,
  output C2,
  output C3,
  output C4,
  output C5,
  output C6,
  output C7
);

  not not_1 (C0, A0);
  not not_2 (C1, A1);
  not not_3 (C2, A2);
  not not_4 (C3, A3);
  not not_5 (C4, A4);
  not not_6 (C5, A5);
  not not_7 (C6, A6);
  not not_8 (C7, A7);
endmodule

module ADD (
  input  A3,
  input  A2,
  input  A1,
  input  A0,
  input  B3,
  input  B2,
  input  B1,
  input  B0,
  input  Cin,
  output out_10,
  output out_11,
  output out_12,
  output out_13,
  output Cout
);

  wire carry_look_ahead_1_c1, carry_look_ahead_1_c2, carry_look_ahead_1_c3, pfa_1_g1, pfa_1_p1, pfa_2_g1,
       pfa_2_p1, pfa_3_g1, pfa_3_p1, pfa_4_g1, pfa_4_p1;

  PFA pfa_1 (.A(A3), .B(B3), .C1(carry_look_ahead_1_c3), .S(out_10), .P1(pfa_1_p1), .G1(pfa_1_g1));
  Carry_Look_Ahead carry_look_ahead_1 (
    .P3(pfa_1_p1), .G3(pfa_1_g1), .P2(pfa_2_p1), .G2(pfa_2_g1), .P1(pfa_3_p1), .G1(pfa_3_g1), .P0(pfa_4_p1),
    .C0(Cin), .G0(pfa_4_g1), .C4(Cout), .C3(carry_look_ahead_1_c3), .C2(carry_look_ahead_1_c2),
    .C1(carry_look_ahead_1_c1));
  PFA pfa_2 (.A(A2), .B(B2), .C1(carry_look_ahead_1_c2), .S(out_11), .P1(pfa_2_p1), .G1(pfa_2_g1));
  PFA pfa_3 (.A(A1), .B(B1), .C1(carry_look_ahead_1_c1), .S(out_12), .P1(pfa_3_p1), .G1(pfa_3_g1));
  PFA pfa_4 (.A(A0), .B(B0), .C1(Cin), .S(out_13), .P1(pfa_4_p1), .G1(pfa_4_g1));
endmodule

module PFA (
  input  A,
  input  B,
  input  C1,
  output S,
  output P1,
  output G1
);

  wire xor_1_out;

  xor xor_1 (xor_1_out, A, B);
  xor xor_2 (S, xor_1_out, C1);
  or or_1 (P1, A, B);
  and and_1 (G1, A, B);
endmodule

module Carry_Look_Ahead (
  input  P0,
  input  C0,
  input  G0,
  input  P1,
  input  G1,
  input  P2,
  input  G2,
  input  P3,
  input  G3,
  output C1,
  output C2,
  output C3,
  output C4
);

  wire and_1_out, and_2_out, and_3_out, and_4_out;

  and and_1 (and_1_out, P3, C3);
  or or_1 (C4, and_1_out, G3);
  and and_2 (and_2_out, P2, C2);
  or or_2 (C3, and_2_out, G2);
  and and_3 (and_3_out, P1, C1);
  or or_3 (C2, and_3_out, G1);
  and and_4 (and_4_out, P0, C0);
  or or_4 (C1, and_4_out, G0);
endmodule

module _8BitALU (
);

  // subtraction subtraction_1: pin names not known
endmodule

module SLL (
  input  in_1,
  input  in_2,
  input  in_3,
  input  in_4,
  input  in_5,
  input  in_6,
  input  in_7,
  input  in_8,
  output out_9,
  output out_10,
  output out_11,
  output out_12,
  output out_13,
  output out_14,
  output out_15,
  output out_16
);


  assign out_9 = 1'b0;
  assign out_10 = in_1;
  assign out_11 = in_2;
  assign out_12 = in_3;
  assign out_13 = in_4;
  assign out_14 = in_5;
  assign out_15 = in_6;
  assign out_16 = in_7;
endmodule

module SLR (
  input  in_1,
  input  in_2,
  input  in_3,
  input  in_4,
  input  in_5,
  input  in_6,
  input  in_7,
  input  in_8,
  output out_9,
  output out_10,
  output out_11,
  output out_12,
  output out_13,
  output out_14,
  output out_15,
  output out_16
);


  assign out_9 = in_2;
  assign out_10 = in_3;
  assign out_11 = in_4;
  assign out_12 = in_5;
  assign out_13 = in_6;
  assign out_14 = in_7;
  assign out_15 = in_8;
  assign out_16 = 1'b0;
endmodule
