// Logisim project ALU.circ as structural Verilog: 8 circuits, main circuit main
module main (
  input  Cin,
  output C3,
  output C2,
  output C1,
  output C0
);

  wire A0, A1, A2, A3, Ad0, Ad1, Ad2, Ad3, B0, B1, B2, B3, C4, CIN_t, clock_1_out, go, Reset_out, S0, S1,
       t_ff_1_q, t_ff_2_q, t_ff_3_q, t_ff_4_q;
  wire [11:11] rom_1_data;

  Clock clock_1 (.out(clock_1_out));
  T_Flip_Flop t_ff_1 (.clk(clock_1_out), .T(1'b1), .Q(t_ff_1_q), .Qn(Ad0), .preset(Reset_out), .en(go));  // open: reset
  // Probe on {C4, C3, C2, C1, C0}
  T_Flip_Flop t_ff_2 (.clk(t_ff_1_q), .T(1'b1), .Q(t_ff_2_q), .Qn(Ad1), .preset(Reset_out));  // open: reset, en
  // Probe on CIN_t
  // Probe on {S1, S0}
  TTY #(.rows(1), .cols(16)) tty_1 (.data({2'b10, C4, C3, C2, C1, C0}), .clk(clock_1_out), .we(go), .clr(Reset_out));
  T_Flip_Flop t_ff_3 (.clk(t_ff_2_q), .T(1'b1), .Q(t_ff_3_q), .Qn(Ad2), .preset(Reset_out));  // open: reset, en
  ROM #(.addrWidth(4), .dataWidth(12)) rom_1 (
    .addr({Ad3, Ad2, Ad1, Ad0}), .data({rom_1_data[11], CIN_t, S1, S0, B3, B2, B1, B0, A3, A2, A1, A0}));  // open: sel
  // Probe on {B3, B2, B1, B0}
  T_Flip_Flop t_ff_4 (.clk(t_ff_3_q), .T(1'b1), .Q(t_ff_4_q), .Qn(Ad3), .preset(Reset_out));  // open: reset, en
  // Probe on {rom_1_data[11], CIN_t, S1, S0, B3, B2, B1, B0, A3, A2, A1, A0}
  // Probe on {A3, A2, A1, A0}
  Button Reset (.out(Reset_out));
  T_Flip_Flop t_ff_5 (.clk(t_ff_4_q), .T(1'b1), .Q(go), .preset(Reset_out));  // open: Qn, reset, en
  ALU alu_1 (
    .B0(B0), .B1(B1), .B3(B3), .B2(B2), .Cin(CIN_t), .out_12(C3), .out_13(C2), .out_14(C1), .out_15(C0),
    .out_16(C4), .A3(A3), .A2(A2), .A1(A1), .A0(A0), .S1(S1), .S1_2(S0));

  // Notes on the sheet:
  //   adds 64 to make printable
  //   contents of rom_1 (hex, n*v repeats v):
  //   0 4ff ac 100 5ff 1ac 200 6ff 2ac 300 7ff 3ac 3c3 73c 37d 7d7
  //   @_X@_^OPS@_VOPTU
endmodule

module ALU (
  input  S1,
  input  S1_2,
  input  A3,
  input  A2,
  input  A1,
  input  A0,
  input  B3,
  input  B2,
  input  B1,
  input  B0,
  input  Cin,
  output out_12,
  output out_13,
  output out_14,
  output out_15,
  output out_16
);

  wire [3:0] add_1_out_13, and_1_out_9, not_1_c0, or_1_out_9;

  NOT not_1 (
    .A0(A0), .A1(A1), .A2(A2), .A3(A3), .C0(not_1_c0[0]), .C1(not_1_c0[1]), .C2(not_1_c0[2]), .C3(not_1_c0[3]));
  OR or_1 (
    .A0(A0), .B0(B0), .A1(A1), .B1(B1), .A2(A2), .B2(B2), .A3(A3), .B3(B3), .out_9(or_1_out_9[0]),
    .out_10(or_1_out_9[1]), .out_11(or_1_out_9[2]), .out_12(or_1_out_9[3]));
  AND and_1 (
    .A0(A0), .A1(A1), .A2(A2), .A3(A3), .B0(B0), .B1(B1), .B2(B2), .B3(B3), .out_9(and_1_out_9[0]),
    .out_10(and_1_out_9[1]), .out_11(and_1_out_9[2]), .out_12(and_1_out_9[3]));
  ADD add_1 (
    .A0(B0), .B0(A0), .A3(B3), .B3(A3), .A1(B1), .B1(A1), .A2(B2), .B2(A2), .Cin(Cin),
    .out_10(add_1_out_13[3]), .out_11(add_1_out_13[2]), .out_12(add_1_out_13[1]), .out_13(add_1_out_13[0]),
    .Cout(out_16));
  Multiplexer #(.select(2), .width(4)) multiplexer_1 (
    .in0(and_1_out_9), .in1(or_1_out_9), .in2(not_1_c0), .in3(add_1_out_13),
    .out({out_12, out_13, out_14, out_15}), .sel({S1, S1_2}));  // open: en
endmodule

module AND (
  input  A0,
  input  B0,
  input  A1,
  input  B1,
  input  A2,
  input  B2,
  input  A3,
  input  B3,
  output out_9,
  output out_10,
  output out_11,
  output out_12
);

  and and_1 (out_9, A0, B0);
  and and_2 (out_10, A1, B1);
  and and_3 (out_11, A2, B2);
  and and_4 (out_12, A3, B3);
endmodule

module OR (
  input  A0,
  input  B0,
  input  A1,
  input  B1,
  input  A2,
  input  B2,
  input  A3,
  input  B3,
  output out_9,
  output out_10,
  output out_11,
  output out_12
);

  or or_1 (out_9, A0, B0);
  or or_2 (out_10, A1, B1);
  or or_3 (out_11, A2, B2);
  or or_4 (out_12, A3, B3);
endmodule

module NOT (
  input  A0,
  input  A1,
  input  A2,
  input  A3,
  output C0,
  output C1,
  output C2,
  output C3
);

  not not_1 (C0, A0);
  not not_2 (C1, A1);
  not not_3 (C3, A3);
  not not_4 (C2, A2);
endmodule

module ADD (
  input  A3,
  input  A2,
  input  A1,
  input  A0,
  input  B3,
  input  B2,
  input  B1,
  input  B0,
  input  Cin,
  output out_10,
  output out_11,
  output out_12,
  output out_13,
  output Cout
);

  wire carry_look_ahead_1_c1, carry_look_ahead_1_c2, carry_look_ahead_1_c3, pfa_1_g1, pfa_1_p1, pfa_2_g1,
       pfa_2_p1, pfa_3_g1, pfa_3_p1, pfa_4_g1, pfa_4_p1;

  PFA pfa_1 (.A(A3), .B(B3), .C1(carry_look_ahead_1_c3), .S(out_10), .P1(pfa_1_p1), .G1(pfa_1_g1));
  Carry_Look_Ahead carry_look_ahead_1 (
    .P3(pfa_1_p1), .G3(pfa_1_g1), .P2(pfa_2_p1), .G2(pfa_2_g1), .P1(pfa_3_p1), .G1(pfa_3_g1), .P0(pfa_4_p1),
    .C0(Cin), .G0(pfa_4_g1), .C4(Cout), .C3(carry_look_ahead_1_c3), .C2(carry_look_ahead_1_c2),
    .C1(carry_look_ahead_1_c1));
  PFA pfa_2 (.A(A2), .B(B2), .C1(carry_look_ahead_1_c2), .S(out_11), .P1(pfa_2_p1), .G1(pfa_2_g1));
  PFA pfa_3 (.A(A1), .B(B1), .C1(carry_look_ahead_1_c1), .S(out_12), .P1(pfa_3_p1), .G1(pfa_3_g1));
  PFA pfa_4 (.A(A0), .B(B0), .C1(Cin), .S(out_13), .P1(pfa_4_p1), .G1(pfa_4_g1));
endmodule

module PFA (
  input  A,
  input  B,
  input  C1,
  output S,
  output P1,
  output G1
);

  wire xor_1_out;

  xor xor_1 (xor_1_out, A, B);
  xor xor_2 (S, xor_1_out, C1);
  or or_1 (P1, A, B);
  and and_1 (G1, A, B);
endmodule

module Carry_Look_Ahead (
  input  P0,
  input  C0,
  input  G0,
  input  P1,
  input  G1,
  input  P2,
  input  G2,
  input  P3,
  input  G3,
  output C1,
  output C2,
  output C3,
  output C4
);

  wire and_1_out, and_2_out, and_3_out, and_4_out;

  and and_1 (and_1_out, P3, C3);
  or or_1 (C4, and_1_out, G3);
  and and_2 (and_2_out, P2, C2);
  or or_2 (C3, and_2_out, G2);
  and and_3 (and_3_out, P1, C1);
  or or_3 (C2, and_3_out, G1);
  and and_4 (and_4_out, P0, C0);
  or or_4 (C1, and_4_out, G0);
endmodule
