// Logisim project CPU.circ as structural Verilog: 3 circuits, main circuit main
module main (
  input  [4:0] in_1,
  input  in_2,
  input  in_3,
  output out_4
);

  wire [3:0] A_MuxBusControl, B_MuxBusControl, Decoder, Opcode;
  wire [7:0] alu_1_c0, Data, multiplexer_1_out, multiplexer_2_out, register_file_1_r0, register_file_1_r1,
       register_file_1_r2, register_file_1_r3, register_file_1_r4, register_file_1_r5, register_file_1_r6,
       register_file_1_r7, register_file_1_r8;
  wire [8:0] decoder_1_out0;

  Decoder #(.select(4)) decoder_1 (
    .out0(decoder_1_out0[0]), .out1(decoder_1_out0[1]), .out2(decoder_1_out0[2]), .out3(decoder_1_out0[3]),
    .out4(decoder_1_out0[4]), .out5(decoder_1_out0[5]), .out6(decoder_1_out0[6]), .out7(decoder_1_out0[7]),
    .out8(decoder_1_out0[8]), .sel(Decoder));  // open: out9, out10, out11, out12, out13, out14, out15, en
  Register_File register_file_1 (
    .rin(decoder_1_out0), .R0(register_file_1_r0), .R2(register_file_1_r2), .R3(register_file_1_r3),
    .R4(register_file_1_r4), .R1(register_file_1_r1), .R5(register_file_1_r5), .R6(register_file_1_r6),
    .R7(register_file_1_r7), .R8(register_file_1_r8), .din(alu_1_c0));
  RAM #(.addrWidth(5), .dataWidth(24)) ram_1 (
    .addr(in_1), .data({Opcode, Decoder, A_MuxBusControl, B_MuxBusControl, Data}));  // open: sel, clk, ld, clr
  Multiplexer #(.select(4), .width(8)) multiplexer_1 (
    .in0(register_file_1_r0), .in1(register_file_1_r1), .in2(register_file_1_r2), .in3(register_file_1_r3),
    .in4(register_file_1_r4), .in5(register_file_1_r5), .in6(register_file_1_r6), .in7(register_file_1_r7),
    .in8(register_file_1_r8), .out(multiplexer_1_out), .sel(A_MuxBusControl));  // open: in9, in10, in11, in12, in13, in14, in15, en
  ALU alu_1 (
    .B0(multiplexer_2_out[7]), .B1(multiplexer_2_out[6]), .B3(multiplexer_2_out[4]),
    .B2(multiplexer_2_out[5]), .A3(multiplexer_1_out[4]), .A2(multiplexer_1_out[5]),
    .A1(multiplexer_1_out[6]), .A0(multiplexer_1_out[7]), .B7(multiplexer_2_out[0]),
    .B6(multiplexer_2_out[1]), .B5(multiplexer_2_out[2]), .B4(multiplexer_2_out[3]),
    .A7(multiplexer_1_out[0]), .A6(multiplexer_1_out[1]), .A5(multiplexer_1_out[2]),
    .A4(multiplexer_1_out[3]), .D(in_2), .Cin(in_3), .Cout(out_4), .C0(alu_1_c0[0]), .C1(alu_1_c0[1]),
    .C2(alu_1_c0[2]), .C3(alu_1_c0[3]), .C4(alu_1_c0[4]), .C5(alu_1_c0[5]), .C6(alu_1_c0[6]),
    .C7(alu_1_c0[7]), .opCode(Opcode));
  Multiplexer #(.select(4), .width(8)) multiplexer_2 (
    .in0(register_file_1_r0), .in1(register_file_1_r1), .in2(register_file_1_r2), .in3(register_file_1_r3),
    .in4(register_file_1_r4), .in5(register_file_1_r5), .in6(register_file_1_r6), .in7(register_file_1_r7),
    .in8(register_file_1_r8), .in9(Data), .out(multiplexer_2_out), .sel(B_MuxBusControl));  // open: in10, in11, in12, in13, in14, in15, en
endmodule

module Register_File (
  input  [7:0] din,
  input  [8:0] rin,
  output [7:0] R0,
  output [7:0] R1,
  output [7:0] R2,
  output [7:0] R3,
  output [7:0] R4,
  output [7:0] R5,
  output [7:0] R6,
  output [7:0] R7,
  output [7:0] R8
);

  wire c0, c1, c2, c3, c4, c5, c6, c7, c8, Clockin_out, D0, D1, D2, D3, D4, D5, D6, D7, d8, d_ff_9_q,
       d_ff_18_q, d_ff_27_q, d_ff_36_q, d_ff_45_q, d_ff_54_q, d_ff_58_p1, d_ff_63_q, d_ff_72_q, d_ff_81_q;
  wire [8:0] bit_extender_1_out;

  Clock Clockin (.out(Clockin_out));
  D_Flip_Flop d_ff_1 (.clk(c0), .D(din[0]), .Q(R0[0]));  // open: Qn, preset, en, reset
  D_Flip_Flop d_ff_2 (.clk(c0), .D(din[1]), .Q(R0[1]));  // open: Qn, preset, en, reset
  D_Flip_Flop d_ff_3 (.clk(c0), .D(din[2]), .Q(R0[2]));  // open: Qn, preset, en, reset
  D_Flip_Flop d_ff_4 (.clk(c0), .D(din[3]), .Q(R0[3]));  // open: Qn, preset, en, reset
  D_Flip_Flop d_ff_5 (.clk(c0), .D(din[4]), .Q(R0[4]));  // open: Qn, preset, en, reset
  D_Flip_Flop d_ff_6 (.clk(c0), .D(din[5]), .Q(R0[5]));  // open: Qn, preset, en, reset
  D_Flip_Flop d_ff_7 (.clk(c0), .D(din[6]), .Q(R0[6]));  // open: Qn, preset, en, reset
  D_Flip_Flop d_ff_8 (.clk(c0), .D(din[7]), .Q(R0[7]));  // open: Qn, preset, en, reset
  D_Flip_Flop d_ff_9 (.clk(c0), .D(d8), .Q(d_ff_9_q));  // open: Qn, preset, en, reset
  D_Flip_Flop d_ff_10 (.clk(c5), .D(din[0]), .Q(R5[0]));  // open: Qn, preset, en, reset
  D_Flip_Flop d_ff_11 (.clk(c5), .D(din[1]), .Q(R5[1]));  // open: Qn, preset, en, reset
  D_Flip_Flop d_ff_12 (.clk(c5), .D(din[2]), .Q(R5[2]));  // open: Qn, preset, en, reset
  D_Flip_Flop d_ff_13 (.clk(c5), .D(din[3]), .Q(R5[3]));  // open: Qn, preset, en, reset
  D_Flip_Flop d_ff_14 (.clk(c5), .D(din[4]), .Q(R5[4]));  // open: Qn, preset, en, reset
  D_Flip_Flop d_ff_15 (.clk(c5), .D(din[5]), .Q(R5[5]));  // open: Qn, preset, en, reset
  D_Flip_Flop d_ff_16 (.clk(c5), .D(din[6]), .Q(R5[6]));  // open: Qn, preset, en, reset
  D_Flip_Flop d_ff_17 (.clk(c5), .D(din[7]), .Q(R5[7]));  // open: Qn, preset, en, reset
  D_Flip_Flop d_ff_18 (.clk(c5), .D(d8), .Q(d_ff_18_q));  // open: Qn, preset, en, reset
  assign bit_extender_1_out = {{8{1'b1}}, Clockin_out};  // Bit_Extender bit_extender_1
  D_Flip_Flop d_ff_19 (.clk(c1), .D(din[0]), .Q(R1[0]));  // open: Qn, preset, en, reset
  D_Flip_Flop d_ff_20 (.clk(c1), .D(din[1]), .Q(R1[1]));  // open: Qn, preset, en, reset
  D_Flip_Flop d_ff_21 (.clk(c1), .D(din[2]), .Q(R1[2]));  // open: Qn, preset, en, reset
  D_Flip_Flop d_ff_22 (.clk(c1), .D(din[3]), .Q(R1[3]));  // open: Qn, preset, en, reset
  D_Flip_Flop d_ff_23 (.clk(c1), .D(din[4]), .Q(R1[4]));  // open: Qn, preset, en, reset
  D_Flip_Flop d_ff_24 (.clk(c1), .D(din[5]), .Q(R1[5]));  // open: Qn, preset, en, reset
  D_Flip_Flop d_ff_25 (.clk(c1), .D(din[6]), .Q(R1[6]));  // open: Qn, preset, en, reset
  D_Flip_Flop d_ff_26 (.clk(c1), .D(din[7]), .Q(R1[7]));  // open: Qn, preset, en, reset
  D_Flip_Flop d_ff_27 (.clk(c1), .D(d8), .Q(d_ff_27_q));  // open: Qn, preset, en, reset
  D_Flip_Flop d_ff_28 (.clk(c6), .D(din[0]), .Q(R6[0]));  // open: Qn, preset, en, reset
  D_Flip_Flop d_ff_29 (.clk(c6), .D(din[1]), .Q(R6[1]));  // open: Qn, preset, en, reset
  D_Flip_Flop d_ff_30 (.clk(c6), .D(din[2]), .Q(R6[2]));  // open: Qn, preset, en, reset
  D_Flip_Flop d_ff_31 (.clk(c6), .D(din[3]), .Q(R6[3]));  // open: Qn, preset, en, reset
  D_Flip_Flop d_ff_32 (.clk(c6), .D(din[4]), .Q(R6[4]));  // open: Qn, preset, en, reset
  D_Flip_Flop d_ff_33 (.clk(c6), .D(din[5]), .Q(R6[5]));  // open: Qn, preset, en, reset
  D_Flip_Flop d_ff_34 (.clk(c6), .D(din[6]), .Q(R6[6]));  // open: Qn, preset, en, reset
  D_Flip_Flop d_ff_35 (.clk(c6), .D(din[7]), .Q(R6[7]));  // open: Qn, preset, en, reset
  D_Flip_Flop d_ff_36 (.clk(c6), .D(d8), .Q(d_ff_36_q));  // open: Qn, preset, en, reset
  assign {c8, c7, c6, c5, c4, c3, c2, c1, c0} = rin & bit_extender_1_out;  // AND_Gate and_1, 9 bits wide
  D_Flip_Flop d_ff_37 (.clk(c2), .D(din[0]), .Q(R2[0]));  // open: Qn, preset, en, reset
  D_Flip_Flop d_ff_38 (.clk(c2), .D(din[1]), .Q(R2[1]));  // open: Qn, preset, en, reset
  D_Flip_Flop d_ff_39 (.clk(c2), .D(din[2]), .Q(R2[2]));  // open: Qn, preset, en, reset
  D_Flip_Flop d_ff_40 (.clk(c2), .D(din[3]), .Q(R2[3]));  // open: Qn, preset, en, reset
  D_Flip_Flop d_ff_41 (.clk(c2), .D(din[4]), .Q(R2[4]));  // open: Qn, preset, en, reset
  D_Flip_Flop d_ff_42 (.clk(c2), .D(din[5]), .Q(R2[5]));  // open: Qn, preset, en, reset
  D_Flip_Flop d_ff_43 (.clk(c2), .D(din[6]), .Q(R2[6]));  // open: Qn, preset, en, reset
  D_Flip_Flop d_ff_44 (.clk(c2), .D(din[7]), .Q(R2[7]));  // open: Qn, preset, en, reset
  D_Flip_Flop d_ff_45 (.clk(c2), .D(d8), .Q(d_ff_45_q));  // open: Qn, preset, en, reset
  D_Flip_Flop d_ff_46 (.clk(c7), .D(din[0]), .Q(R7[0]));  // open: Qn, preset, en, reset
  D_Flip_Flop d_ff_47 (.clk(c7), .D(din[1]), .Q(R7[1]));  // open: Qn, preset, en, reset
  D_Flip_Flop d_ff_48 (.clk(c7), .D(din[2]), .Q(R7[2]));  // open: Qn, preset, en, reset
  D_Flip_Flop d_ff_49 (.clk(c7), .D(din[3]), .Q(R7[3]));  // open: Qn, preset, en, reset
  D_Flip_Flop d_ff_50 (.clk(c7), .D(din[4]), .Q(R7[4]));  // open: Qn, preset, en, reset
  D_Flip_Flop d_ff_51 (.clk(c7), .D(din[5]), .Q(R7[5]));  // open: Qn, preset, en, reset
  D_Flip_Flop d_ff_52 (.clk(c7), .D(din[6]), .Q(R7[6]));  // open: Qn, preset, en, reset
  D_Flip_Flop d_ff_53 (.clk(c7), .D(din[7]), .Q(R7[7]));  // open: Qn, preset, en, reset
  D_Flip_Flop d_ff_54 (.clk(c7), .D(d8), .Q(d_ff_54_q));  // open: Qn, preset, en, reset
  D_Flip_Flop d_ff_55 (.clk(c3), .D(din[0]), .Q(R3[0]));  // open: Qn, preset, en, reset
  D_Flip_Flop d_ff_56 (.clk(c3), .D(din[1]), .Q(R3[1]));  // open: Qn, preset, en, reset
  D_Flip_Flop d_ff_57 (.clk(c3), .D(din[2]), .Q(R3[2]));  // open: Qn, preset, en, reset
  // D_Flip_Flop d_ff_58: pin names not known; wires that end beside it: d_ff_58_p1, din[3], c3, d_ff_58_p1, R3[3]
  D_Flip_Flop d_ff_59 (.clk(c3), .D(din[4]), .Q(R3[4]));  // open: Qn, preset, en, reset
  D_Flip_Flop d_ff_60 (.clk(c3), .D(din[5]), .Q(R3[5]));  // open: Qn, preset, en, reset
  D_Flip_Flop d_ff_61 (.clk(c3), .D(din[6]), .Q(R3[6]));  // open: Qn, preset, en, reset
  D_Flip_Flop d_ff_62 (.clk(c3), .D(din[7]), .Q(R3[7]));  // open: Qn, preset, en, reset
  D_Flip_Flop d_ff_63 (.clk(c3), .D(d8), .Q(d_ff_63_q));  // open: Qn, preset, en, reset
  D_Flip_Flop d_ff_64 (.clk(c8), .D(din[0]), .Q(R8[0]));  // open: Qn, preset, en, reset
  D_Flip_Flop d_ff_65 (.clk(c8), .D(din[1]), .Q(R8[1]));  // open: Qn, preset, en, reset
  D_Flip_Flop d_ff_66 (.clk(c8), .D(din[2]), .Q(R8[2]));  // open: Qn, preset, en, reset
  D_Flip_Flop d_ff_67 (.clk(c8), .D(din[3]), .Q(R8[3]));  // open: Qn, preset, en, reset
  D_Flip_Flop d_ff_68 (.clk(c8), .D(din[4]), .Q(R8[4]));  // open: Qn, preset, en, reset
  D_Flip_Flop d_ff_69 (.clk(c8), .D(din[5]), .Q(R8[5]));  // open: Qn, preset, en, reset
  D_Flip_Flop d_ff_70 (.clk(c8), .D(din[6]), .Q(R8[6]));  // open: Qn, preset, en, reset
  D_Flip_Flop d_ff_71 (.clk(c8), .D(din[7]), .Q(R8[7]));  // open: Qn, preset, en, reset
  D_Flip_Flop d_ff_72 (.clk(c8), .D(d8), .Q(d_ff_72_q));  // open: Qn, preset, en, reset
  D_Flip_Flop d_ff_73 (.clk(c4), .D(din[0]), .Q(R4[0]));  // open: Qn, preset, en, reset
  D_Flip_Flop d_ff_74 (.clk(c4), .D(din[1]), .Q(R4[1]));  // open: Qn, preset, en, reset
  D_Flip_Flop d_ff_75 (.clk(c4), .D(din[2]), .Q(R4[2]));  // open: Qn, preset, en, reset
  D_Flip_Flop d_ff_76 (.clk(c4), .D(din[3]), .Q(R4[3]));  // open: Qn, preset, en, reset
  D_Flip_Flop d_ff_77 (.clk(c4), .D(din[4]), .Q(R4[4]));  // open: Qn, preset, en, reset
  D_Flip_Flop d_ff_78 (.clk(c4), .D(din[5]), .Q(R4[5]));  // open: Qn, preset, en, reset
  D_Flip_Flop d_ff_79 (.clk(c4), .D(din[6]), .Q(R4[6]));  // open: Qn, preset, en, reset
  D_Flip_Flop d_ff_80 (.clk(c4), .D(din[7]), .Q(R4[7]));  // open: Qn, preset, en, reset
  D_Flip_Flop d_ff_81 (.clk(c4), .D(d8), .Q(d_ff_81_q));  // open: Qn, preset, en, reset
  D_Flip_Flop d_ff_82 (.D(din[0]), .Q(D0));  // open: clk, Qn, preset, en, reset
  D_Flip_Flop d_ff_83 (.D(din[1]), .Q(D1));  // open: clk, Qn, preset, en, reset
  D_Flip_Flop d_ff_84 (.D(din[2]), .Q(D2));  // open: clk, Qn, preset, en, reset
  D_Flip_Flop d_ff_85 (.D(din[3]), .Q(D3));  // open: clk, Qn, preset, en, reset
  D_Flip_Flop d_ff_86 (.D(din[4]), .Q(D4));  // open: clk, Qn, preset, en, reset
  D_Flip_Flop d_ff_87 (.D(din[5]), .Q(D5));  // open: clk, Qn, preset, en, reset
  D_Flip_Flop d_ff_88 (.D(din[6]), .Q(D6));  // open: clk, Qn, preset, en, reset
  D_Flip_Flop d_ff_89 (.D(din[7]), .Q(D7));  // open: clk, Qn, preset, en, reset

  // Other names for the same wires on the sheet: d0_t = din[0]; d1_t = din[1]; d2_t = din[2]; d3_t = din[3];
  //   d4_t = din[4]; d5_t = din[5]; d6_t = din[6]; d7_t = din[7]

  // Notes on the sheet:
  //   Unit to select the reigster
  //   data to feed into the register
endmodule

module clockExtension (
  input  in_1,
  output out_2,
  output out_3,
  output out_4,
  output out_5,
  output out_6,
  output out_7,
  output out_8,
  output out_9
);


  assign out_2 = in_1;
  assign out_3 = in_1;
  assign out_4 = in_1;
  assign out_5 = in_1;
  assign out_6 = in_1;
  assign out_7 = in_1;
  assign out_8 = in_1;
  assign out_9 = in_1;
endmodule
