// Logisim project CPUnew1.circ as structural Verilog: 14 circuits, main circuit main
module main (
  input  [4:0] in_1,
  input  in_2,
  input  in_3
);

  wire clock_1_out, comparator_1_lt, comparator_2_lt, counter_1_carry, not_1_out, Reset, TClock;
  wire [3:0] A_MuxBusControl, B, B_MuxBusControl, Decoder, Opcode, rom_1_data;
  wire [4:0] counter_1_q, pc_counter_1_out_3;
  wire [6:0] adder_1_out, adder_2_out, LSB, MSB;
  wire [7:0] Data, multiplexer_1_out, multiplexer_2_out, multiplexer_3_out, n8bitalu_1_c0, R0, R1, R2, R3,
       R4, R5, R6, R7, R8;
  wire [8:0] decoder_1_out0;

  PC_Counter pc_counter_1 (.in_1(TClock), .out_3(pc_counter_1_out_3), .in_2(Opcode));
  Decoder #(.select(4)) decoder_1 (
    .out0(decoder_1_out0[0]), .out1(decoder_1_out0[1]), .out2(decoder_1_out0[2]), .out3(decoder_1_out0[3]),
    .out4(decoder_1_out0[4]), .out5(decoder_1_out0[5]), .out6(decoder_1_out0[6]), .out7(decoder_1_out0[7]),
    .out8(decoder_1_out0[8]), .sel(Decoder));  // open: out9, out10, out11, out12, out13, out14, out15, en
  Register_File register_file_1 (
    .rin(decoder_1_out0), .R0(R0), .R2(R2), .R3(R3), .R4(R4), .R1(R1), .R5(R5), .R6(R6), .R7(R7), .R8(R8),
    .din(n8bitalu_1_c0), .TClock(TClock));
  RAM #(.addrWidth(5), .dataWidth(24)) ram_1 (
    .addr(pc_counter_1_out_3), .data({Opcode, Decoder, A_MuxBusControl, B_MuxBusControl, Data}));  // open: sel, clk, ld, clr
  Multiplexer #(.select(4), .width(8)) multiplexer_1 (
    .in0(R0), .in1(R1), .in2(R2), .in3(R3), .in4(R4), .in5(R5), .in6(R6), .in7(R7), .in8(R8),
    .out(multiplexer_1_out), .sel(A_MuxBusControl));  // open: in9, in10, in11, in12, in13, in14, in15, en
  _8bitALU u_8bitalu_1 (
    .A(multiplexer_1_out), .B(multiplexer_2_out), .Cin(in_3), .C0(n8bitalu_1_c0[0]), .C1(n8bitalu_1_c0[1]),
    .C2(n8bitalu_1_c0[2]), .C3(n8bitalu_1_c0[3]), .C4(n8bitalu_1_c0[4]), .C5(n8bitalu_1_c0[5]),
    .C6(n8bitalu_1_c0[6]), .C7(n8bitalu_1_c0[7]), .opCode(Opcode));
  Immediate Immediate (.Opcode(Opcode), .Bmux(B_MuxBusControl), .Output_BMux(B));
  Multiplexer #(.select(4), .width(8)) multiplexer_2 (
    .in0(R0), .in1(R1), .in2(R2), .in3(R3), .in4(R4), .in5(R5), .in6(R6), .in7(R7), .in8(R8), .in9(Data),
    .out(multiplexer_2_out), .sel(B));  // open: in10, in11, in12, in13, in14, in15, en
  TTY #(.rows(33), .cols(1)) tty_1 (.data(MSB), .clk(TClock), .clr(Reset));  // open: we
  TTY #(.rows(33), .cols(1)) tty_2 (.data(LSB), .clk(TClock), .clr(Reset));  // open: we
  Button u_Reset (.out(Reset));
  Counter #(.width(5), .max('h1f)) counter_1 (
    .Q(counter_1_q), .carry(counter_1_carry), .clk(TClock), .clr(Reset));  // open: load, D, count
  Multiplexer #(.select(4), .width(8), .disabled(0), .enable("false")) multiplexer_3 (
    .in0(R0), .in1(R1), .in2(R2), .in3(R3), .in4(R4), .in5(R5), .in6(R6), .in7(R7), .in8(R8),
    .out(multiplexer_3_out), .sel(rom_1_data));  // open: in9, in10, in11, in12, in13, in14, in15
  not not_1 (not_1_out, counter_1_carry);
  Clock clock_1 (.out(clock_1_out));
  ROM #(.addrWidth(5), .dataWidth(4)) rom_1 (.addr(counter_1_q), .data(rom_1_data));  // open: sel
  and and_1 (TClock, not_1_out, clock_1_out);
  Comparator #(.width(7)) comparator_1 (
    .a(7'b0111001), .b({3'b011, multiplexer_3_out[3:0]}), .lt(comparator_1_lt));  // open: gt, eq
  Comparator #(.width(7)) comparator_2 (
    .a(7'b0111001), .b({3'b011, multiplexer_3_out[7:4]}), .lt(comparator_2_lt));  // open: gt, eq
  Adder #(.width(7)) adder_1 (
    .a({3'b011, multiplexer_3_out[3:0]}), .b(7'b0000111), .out(adder_1_out));  // open: cin, cout
  Adder #(.width(7)) adder_2 (
    .a({3'b011, multiplexer_3_out[7:4]}), .b(7'b0000111), .out(adder_2_out));  // open: cin, cout
  Multiplexer #(.width(7), .disabled(0), .enable("false")) multiplexer_4 (
    .in0({3'b011, multiplexer_3_out[3:0]}), .in1(adder_1_out), .out(LSB), .sel(comparator_1_lt));
  Multiplexer #(.width(7), .disabled(0), .enable("false")) multiplexer_5 (
    .in0({3'b011, multiplexer_3_out[7:4]}), .in1(adder_2_out), .out(MSB), .sel(comparator_2_lt));

  // Notes on the sheet:
  //   00
  //   F5
  //   5A
  //   50
  //   FF
  //   0A
  //   4F
  //   F5
  //   EA
  //   7A
  //   9B
  //   65
  //   0F
  //   FF
  //   F5
  //   AA
  //   5A
  //   0A
  //   FA
  //   A5
  //   04
  //   5A
  //   B4
  //   2D
  //   0A
  //   B0
  //   50
  //   0F
  //   00
  //   00
  //   5A
  //   contents of rom_1 (hex, n*v repeats v):
  //   0 0 1 2 3 4 5 6 7 8 2 3 4 5 0 0 1 6 7 8 2 3 4 5 6 6 7 8 2 3 4 4
endmodule

module Register_File (
  input  [7:0] din,
  input  [8:0] rin,
  input  TClock,
  output [7:0] R0,
  output [7:0] R1,
  output [7:0] R2,
  output [7:0] R3,
  output [7:0] R4,
  output [7:0] R5,
  output [7:0] R6,
  output [7:0] R7,
  output [7:0] R8
);

  wire c0, c1, c2, c3, c4, c5, c6, c7, c8, D0, D1, D2, D3, D4, D5, D6, D7, d8, d_ff_9_q, d_ff_18_q,
       d_ff_27_q, d_ff_36_q, d_ff_45_q, d_ff_54_q, d_ff_63_q, d_ff_72_q, d_ff_81_q;
  wire [8:0] bit_extender_1_out;

  Clock Clockin ();  // open: out
  D_Flip_Flop d_ff_1 (.clk(c0), .D(din[0]), .Q(R0[0]));  // open: Qn, preset, en, reset
  D_Flip_Flop d_ff_2 (.clk(c0), .D(din[1]), .Q(R0[1]));  // open: Qn, preset, en, reset
  D_Flip_Flop d_ff_3 (.clk(c0), .D(din[2]), .Q(R0[2]));  // open: Qn, preset, en, reset
  D_Flip_Flop d_ff_4 (.clk(c0), .D(din[3]), .Q(R0[3]));  // open: Qn, preset, en, reset
  D_Flip_Flop d_ff_5 (.clk(c0), .D(din[4]), .Q(R0[4]));  // open: Qn, preset, en, reset
  D_Flip_Flop d_ff_6 (.clk(c0), .D(din[5]), .Q(R0[5]));  // open: Qn, preset, en, reset
  D_Flip_Flop d_ff_7 (.clk(c0), .D(din[6]), .Q(R0[6]));  // open: Qn, preset, en, reset
  D_Flip_Flop d_ff_8 (.clk(c0), .D(din[7]), .Q(R0[7]));  // open: Qn, preset, en, reset
  D_Flip_Flop d_ff_9 (.clk(c0), .D(d8), .Q(d_ff_9_q));  // open: Qn, preset, en, reset
  D_Flip_Flop d_ff_10 (.clk(c5), .D(din[0]), .Q(R5[0]));  // open: Qn, preset, en, reset
  D_Flip_Flop d_ff_11 (.clk(c5), .D(din[1]), .Q(R5[1]));  // open: Qn, preset, en, reset
  D_Flip_Flop d_ff_12 (.clk(c5), .D(din[2]), .Q(R5[2]));  // open: Qn, preset, en, reset
  D_Flip_Flop d_ff_13 (.clk(c5), .D(din[3]), .Q(R5[3]));  // open: Qn, preset, en, reset
  D_Flip_Flop d_ff_14 (.clk(c5), .D(din[4]), .Q(R5[4]));  // open: Qn, preset, en, reset
  D_Flip_Flop d_ff_15 (.clk(c5), .D(din[5]), .Q(R5[5]));  // open: Qn, preset, en, reset
  D_Flip_Flop d_ff_16 (.clk(c5), .D(din[6]), .Q(R5[6]));  // open: Qn, preset, en, reset
  D_Flip_Flop d_ff_17 (.clk(c5), .D(din[7]), .Q(R5[7]));  // open: Qn, preset, en, reset
  D_Flip_Flop d_ff_18 (.clk(c5), .D(d8), .Q(d_ff_18_q));  // open: Qn, preset, en, reset
  assign bit_extender_1_out = {{8{TClock}}, TClock};  // Bit_Extender bit_extender_1
  D_Flip_Flop d_ff_19 (.clk(c1), .D(din[0]), .Q(R1[0]));  // open: Qn, preset, en, reset
  D_Flip_Flop d_ff_20 (.clk(c1), .D(din[1]), .Q(R1[1]));  // open: Qn, preset, en, reset
  D_Flip_Flop d_ff_21 (.clk(c1), .D(din[2]), .Q(R1[2]));  // open: Qn, preset, en, reset
  D_Flip_Flop d_ff_22 (.clk(c1), .D(din[3]), .Q(R1[3]));  // open: Qn, preset, en, reset
  D_Flip_Flop d_ff_23 (.clk(c1), .D(din[4]), .Q(R1[4]));  // open: Qn, preset, en, reset
  D_Flip_Flop d_ff_24 (.clk(c1), .D(din[5]), .Q(R1[5]));  // open: Qn, preset, en, reset
  D_Flip_Flop d_ff_25 (.clk(c1), .D(din[6]), .Q(R1[6]));  // open: Qn, preset, en, reset
  D_Flip_Flop d_ff_26 (.clk(c1), .D(din[7]), .Q(R1[7]));  // open: Qn, preset, en, reset
  D_Flip_Flop d_ff_27 (.clk(c1), .D(d8), .Q(d_ff_27_q));  // open: Qn, preset, en, reset
  D_Flip_Flop d_ff_28 (.clk(c6), .D(din[0]), .Q(R6[0]));  // open: Qn, preset, en, reset
  D_Flip_Flop d_ff_29 (.clk(c6), .D(din[1]), .Q(R6[1]));  // open: Qn, preset, en, reset
  D_Flip_Flop d_ff_30 (.clk(c6), .D(din[2]), .Q(R6[2]));  // open: Qn, preset, en, reset
  D_Flip_Flop d_ff_31 (.clk(c6), .D(din[3]), .Q(R6[3]));  // open: Qn, preset, en, reset
  D_Flip_Flop d_ff_32 (.clk(c6), .D(din[4]), .Q(R6[4]));  // open: Qn, preset, en, reset
  D_Flip_Flop d_ff_33 (.clk(c6), .D(din[5]), .Q(R6[5]));  // open: Qn, preset, en, reset
  D_Flip_Flop d_ff_34 (.clk(c6), .D(din[6]), .Q(R6[6]));  // open: Qn, preset, en, reset
  D_Flip_Flop d_ff_35 (.clk(c6), .D(din[7]), .Q(R6[7]));  // open: Qn, preset, en, reset
  D_Flip_Flop d_ff_36 (.clk(c6), .D(d8), .Q(d_ff_36_q));  // open: Qn, preset, en, reset
  assign {c8, c7, c6, c5, c4, c3, c2, c1, c0} = rin & bit_extender_1_out;  // AND_Gate and_1, 9 bits wide
  D_Flip_Flop d_ff_37 (.clk(c2), .D(din[0]), .Q(R2[0]));  // open: Qn, preset, en, reset
  D_Flip_Flop d_ff_38 (.clk(c2), .D(din[1]), .Q(R2[1]));  // open: Qn, preset, en, reset
  D_Flip_Flop d_ff_39 (.clk(c2), .D(din[2]), .Q(R2[2]));  // open: Qn, preset, en, reset
  D_Flip_Flop d_ff_40 (.clk(c2), .D(din[3]), .Q(R2[3]));  // open: Qn, preset, en, reset
  D_Flip_Flop d_ff_41 (.clk(c2), .D(din[4]), .Q(R2[4]));  // open: Qn, preset, en, reset
  D_Flip_Flop d_ff_42 (.clk(c2), .D(din[5]), .Q(R2[5]));  // open: Qn, preset, en, reset
  D_Flip_Flop d_ff_43 (.clk(c2), .D(din[6]), .Q(R2[6]));  // open: Qn, preset, en, reset
  D_Flip_Flop d_ff_44 (.clk(c2), .D(din[7]), .Q(R2[7]));  // open: Qn, preset, en, reset
  D_Flip_Flop d_ff_45 (.clk(c2), .D(d8), .Q(d_ff_45_q));  // open: Qn, preset, en, reset
  D_Flip_Flop d_ff_46 (.clk(c7), .D(din[0]), .Q(R7[0]));  // open: Qn, preset, en, reset
  D_Flip_Flop d_ff_47 (.clk(c7), .D(din[1]), .Q(R7[1]));  // open: Qn, preset, en, reset
  D_Flip_Flop d_ff_48 (.clk(c7), .D(din[2]), .Q(R7[2]));  // open: Qn, preset, en, reset
  D_Flip_Flop d_ff_49 (.clk(c7), .D(din[3]), .Q(R7[3]));  // open: Qn, preset, en, reset
  D_Flip_Flop d_ff_50 (.clk(c7), .D(din[4]), .Q(R7[4]));  // open: Qn, preset, en, reset
  D_Flip_Flop d_ff_51 (.clk(c7), .D(din[5]), .Q(R7[5]));  // open: Qn, preset, en, reset
  D_Flip_Flop d_ff_52 (.clk(c7), .D(din[6]), .Q(R7[6]));  // open: Qn, preset, en, reset
  D_Flip_Flop d_ff_53 (.clk(c7), .D(din[7]), .Q(R7[7]));  // open: Qn, preset, en, reset
  D_Flip_Flop d_ff_54 (.clk(c7), .D(d8), .Q(d_ff_54_q));  // open: Qn, preset, en, reset
  D_Flip_Flop d_ff_55 (.clk(c3), .D(din[0]), .Q(R3[0]));  // open: Qn, preset, en, reset
  D_Flip_Flop d_ff_56 (.clk(c3), .D(din[1]), .Q(R3[1]));  // open: Qn, preset, en, reset
  D_Flip_Flop d_ff_57 (.clk(c3), .D(din[2]), .Q(R3[2]));  // open: Qn, preset, en, reset
  D_Flip_Flop d_ff_58 (.clk(c3), .D(din[3]), .Q(R3[3]));  // open: Qn, preset, en, reset
  D_Flip_Flop d_ff_59 (.clk(c3), .D(din[4]), .Q(R3[4]));  // open: Qn, preset, en, reset
  D_Flip_Flop d_ff_60 (.clk(c3), .D(din[5]), .Q(R3[5]));  // open: Qn, preset, en, reset
  D_Flip_Flop d_ff_61 (.clk(c3), .D(din[6]), .Q(R3[6]));  // open: Qn, preset, en, reset
  D_Flip_Flop d_ff_62 (.clk(c3), .D(din[7]), .Q(R3[7]));  // open: Qn, preset, en, reset
  D_Flip_Flop d_ff_63 (.clk(c3), .D(d8), .Q(d_ff_63_q));  // open: Qn, preset, en, reset
  D_Flip_Flop d_ff_64 (.clk(c8), .D(din[0]), .Q(R8[0]));  // open: Qn, preset, en, reset
  D_Flip_Flop d_ff_65 (.clk(c8), .D(din[1]), .Q(R8[1]));  // open: Qn, preset, en, reset
  D_Flip_Flop d_ff_66 (.clk(c8), .D(din[2]), .Q(R8[2]));  // open: Qn, preset, en, reset
  D_Flip_Flop d_ff_67 (.clk(c8), .D(din[3]), .Q(R8[3]));  // open: Qn, preset, en, reset
  D_Flip_Flop d_ff_68 (.clk(c8), .D(din[4]), .Q(R8[4]));  // open: Qn, preset, en, reset
  D_Flip_Flop d_ff_69 (.clk(c8), .D(din[5]), .Q(R8[5]));  // open: Qn, preset, en, reset
  D_Flip_Flop d_ff_70 (.clk(c8), .D(din[6]), .Q(R8[6]));  // open: Qn, preset, en, reset
  D_Flip_Flop d_ff_71 (.clk(c8), .D(din[7]), .Q(R8[7]));  // open: Qn, preset, en, reset
  D_Flip_Flop d_ff_72 (.clk(c8), .D(d8), .Q(d_ff_72_q));  // open: Qn, preset, en, reset
  D_Flip_Flop d_ff_73 (.clk(c4), .D(din[0]), .Q(R4[0]));  // open: Qn, preset, en, reset
  D_Flip_Flop d_ff_74 (.clk(c4), .D(din[1]), .Q(R4[1]));  // open: Qn, preset, en, reset
  D_Flip_Flop d_ff_75 (.clk(c4), .D(din[2]), .Q(R4[2]));  // open: Qn, preset, en, reset
  D_Flip_Flop d_ff_76 (.clk(c4), .D(din[3]), .Q(R4[3]));  // open: Qn, preset, en, reset
  D_Flip_Flop d_ff_77 (.clk(c4), .D(din[4]), .Q(R4[4]));  // open: Qn, preset, en, reset
  D_Flip_Flop d_ff_78 (.clk(c4), .D(din[5]), .Q(R4[5]));  // open: Qn, preset, en, reset
  D_Flip_Flop d_ff_79 (.clk(c4), .D(din[6]), .Q(R4[6]));  // open: Qn, preset, en, reset
  D_Flip_Flop d_ff_80 (.clk(c4), .D(din[7]), .Q(R4[7]));  // open: Qn, preset, en, reset
  D_Flip_Flop d_ff_81 (.clk(c4), .D(d8), .Q(d_ff_81_q));  // open: Qn, preset, en, reset
  D_Flip_Flop d_ff_82 (.D(din[0]), .Q(D0));  // open: clk, Qn, preset, en, reset
  D_Flip_Flop d_ff_83 (.D(din[1]), .Q(D1));  // open: clk, Qn, preset, en, reset
  D_Flip_Flop d_ff_84 (.D(din[2]), .Q(D2));  // open: clk, Qn, preset, en, reset
  D_Flip_Flop d_ff_85 (.D(din[3]), .Q(D3));  // open: clk, Qn, preset, en, reset
  D_Flip_Flop d_ff_86 (.D(din[4]), .Q(D4));  // open: clk, Qn, preset, en, reset
  D_Flip_Flop d_ff_87 (.D(din[5]), .Q(D5));  // open: clk, Qn, preset, en, reset
  D_Flip_Flop d_ff_88 (.D(din[6]), .Q(D6));  // open: clk, Qn, preset, en, reset
  D_Flip_Flop d_ff_89 (.D(din[7]), .Q(D7));  // open: clk, Qn, preset, en, reset

  // Other names for the same wires on the sheet: d0_t = din[0]; d1_t = din[1]; d2_t = din[2]; d3_t = din[3];
  //   d4_t = din[4]; d5_t = din[5]; d6_t = din[6]; d7_t = din[7]

  // Notes on the sheet:
  //   Unit to select the reigster
  //   data to feed into the register
endmodule

module clockExtension (
  input  in_1,
  output out_2,
  output out_3,
  output out_4,
  output out_5,
  output out_6,
  output out_7,
  output out_8,
  output out_9
);


  assign out_2 = in_1;
  assign out_3 = in_1;
  assign out_4 = in_1;
  assign out_5 = in_1;
  assign out_6 = in_1;
  assign out_7 = in_1;
  assign out_8 = in_1;
  assign out_9 = in_1;
endmodule

module _8bitALU (
  input  [7:0] A,
  input  [7:0] B,
  input  [3:0] opCode,
  input  Cin,
  output C0,
  output C1,
  output C2,
  output C3,
  output C4,
  output C5,
  output C6,
  output C7
);

  wire undriven;
  wire [7:0] ADD_SUB_2_s0, ADD_SUB_s0, AND_out_17, NOT_c0, OR_out_17, SLL_out_9, SLR_out_9;

  Add_Sub ADD_SUB (
    .D(1'b0), .Cin(Cin), .A7(A[7]), .B7(B[7]), .A6(A[6]), .B6(B[6]), .A5(A[5]), .B5(B[5]), .A4(A[4]),
    .B4(B[4]), .A3(A[3]), .B3(B[3]), .A2(A[2]), .B2(B[2]), .A1(A[1]), .B1(B[1]), .A0(A[0]), .B0(B[0]),
    .S7(ADD_SUB_s0[7]), .S6(ADD_SUB_s0[6]), .S5(ADD_SUB_s0[5]), .S4(ADD_SUB_s0[4]), .S3(ADD_SUB_s0[3]),
    .S2(ADD_SUB_s0[2]), .S1(ADD_SUB_s0[1]), .S0(ADD_SUB_s0[0]));  // open: C8
  Add_Sub ADD_SUB_2 (
    .D(1'b1), .Cin(undriven), .A7(B[7]), .B7(A[7]), .A6(B[6]), .B6(A[6]), .A5(B[5]), .B5(A[5]), .A4(B[4]),
    .B4(A[4]), .A3(B[3]), .B3(A[3]), .A2(B[2]), .B2(A[2]), .A1(B[1]), .B1(A[1]), .A0(B[0]), .B0(A[0]),
    .S7(ADD_SUB_2_s0[7]), .S6(ADD_SUB_2_s0[6]), .S5(ADD_SUB_2_s0[5]), .S4(ADD_SUB_2_s0[4]),
    .S3(ADD_SUB_2_s0[3]), .S2(ADD_SUB_2_s0[2]), .S1(ADD_SUB_2_s0[1]), .S0(ADD_SUB_2_s0[0]));  // open: C8
  SLR SLR (
    .in_1(A[0]), .in_2(A[1]), .in_3(A[2]), .in_4(A[3]), .in_5(A[4]), .in_6(A[5]), .in_7(A[6]), .in_8(A[7]),
    .out_9(SLR_out_9[0]), .out_10(SLR_out_9[1]), .out_11(SLR_out_9[2]), .out_12(SLR_out_9[3]),
    .out_13(SLR_out_9[4]), .out_14(SLR_out_9[5]), .out_15(SLR_out_9[6]), .out_16(SLR_out_9[7]));
  SLL SLL (
    .in_1(A[0]), .in_2(A[1]), .in_3(A[2]), .in_4(A[3]), .in_5(A[4]), .in_6(A[5]), .in_7(A[6]), .in_8(A[7]),
    .out_9(SLL_out_9[0]), .out_10(SLL_out_9[1]), .out_11(SLL_out_9[2]), .out_12(SLL_out_9[3]),
    .out_13(SLL_out_9[4]), .out_14(SLL_out_9[5]), .out_15(SLL_out_9[6]), .out_16(SLL_out_9[7]));
  AND AND (
    .A0(A[0]), .B0(B[0]), .A1(A[1]), .B1(B[1]), .A2(A[2]), .B2(B[2]), .A3(A[3]), .B3(B[3]), .A4(A[4]),
    .B4(B[4]), .A5(A[5]), .B5(B[5]), .A6(A[6]), .B6(B[6]), .A7(A[7]), .B7(B[7]), .out_17(AND_out_17[0]),
    .out_18(AND_out_17[1]), .out_19(AND_out_17[2]), .out_20(AND_out_17[3]), .out_21(AND_out_17[4]),
    .out_22(AND_out_17[5]), .out_23(AND_out_17[6]), .out_24(AND_out_17[7]));
  OR OR (
    .A0(A[0]), .B0(B[0]), .A1(A[1]), .B1(B[1]), .A2(A[2]), .B2(B[2]), .A3(A[3]), .B3(B[3]), .A4(A[4]),
    .B4(B[4]), .A5(A[5]), .B5(B[5]), .A6(A[6]), .B6(B[6]), .A7(A[7]), .B7(B[7]), .out_17(OR_out_17[0]),
    .out_18(OR_out_17[1]), .out_19(OR_out_17[2]), .out_20(OR_out_17[3]), .out_21(OR_out_17[4]),
    .out_22(OR_out_17[5]), .out_23(OR_out_17[6]), .out_24(OR_out_17[7]));
  NOT NOT (
    .A0(A[0]), .A1(A[1]), .A2(A[2]), .A3(A[3]), .A4(A[4]), .A5(A[5]), .A6(A[6]), .A7(A[7]), .C0(NOT_c0[0]),
    .C1(NOT_c0[1]), .C2(NOT_c0[2]), .C3(NOT_c0[3]), .C4(NOT_c0[4]), .C5(NOT_c0[5]), .C6(NOT_c0[6]),
    .C7(NOT_c0[7]));
  Multiplexer #(.select(4), .width(8)) multiplexer_1 (
    .in0(AND_out_17), .in1(OR_out_17), .in2(NOT_c0), .in3(ADD_SUB_s0), .in4(A), .in5(SLL_out_9),
    .in6(SLR_out_9), .in7(ADD_SUB_2_s0), .in8(ADD_SUB_s0), .in9(ADD_SUB_2_s0), .in10(B),
    .out({C7, C6, C5, C4, C3, C2, C1, C0}), .sel(opCode));  // open: in11, in12, in13, in14, in15, en
endmodule

module SLR (
  input  in_1,
  input  in_2,
  input  in_3,
  input  in_4,
  input  in_5,
  input  in_6,
  input  in_7,
  input  in_8,
  output out_9,
  output out_10,
  output out_11,
  output out_12,
  output out_13,
  output out_14,
  output out_15,
  output out_16
);


  assign out_9 = in_2;
  assign out_10 = in_3;
  assign out_11 = in_4;
  assign out_12 = in_5;
  assign out_13 = in_6;
  assign out_14 = in_7;
  assign out_15 = in_8;
  assign out_16 = 1'b0;
endmodule

module SLL (
  input  in_1,
  input  in_2,
  input  in_3,
  input  in_4,
  input  in_5,
  input  in_6,
  input  in_7,
  input  in_8,
  output out_9,
  output out_10,
  output out_11,
  output out_12,
  output out_13,
  output out_14,
  output out_15,
  output out_16
);


  assign out_9 = 1'b0;
  assign out_10 = in_1;
  assign out_11 = in_2;
  assign out_12 = in_3;
  assign out_13 = in_4;
  assign out_14 = in_5;
  assign out_15 = in_6;
  assign out_16 = in_7;
endmodule

module AND (
  input  A0,
  input  B0,
  input  A1,
  input  B1,
  input  A2,
  input  B2,
  input  A3,
  input  B3,
  input  A4,
  input  B4,
  input  A5,
  input  B5,
  input  A6,
  input  B6,
  input  A7,
  input  B7,
  output out_17,
  output out_18,
  output out_19,
  output out_20,
  output out_21,
  output out_22,
  output out_23,
  output out_24
);

  and and_1 (out_17, A0, B0);
  and and_2 (out_18, A1, B1);
  and and_3 (out_19, A2, B2);
  and and_4 (out_20, A3, B3);
  and and_5 (out_21, A4, B4);
  and and_6 (out_22, A5, B5);
  and and_7 (out_23, A6, B6);
  and and_8 (out_24, A7, B7);
endmodule

module OR (
  input  A0,
  input  B0,
  input  A1,
  input  B1,
  input  A2,
  input  B2,
  input  A3,
  input  B3,
  input  A4,
  input  B4,
  input  A5,
  input  B5,
  input  A6,
  input  B6,
  input  A7,
  input  B7,
  output out_17,
  output out_18,
  output out_19,
  output out_20,
  output out_21,
  output out_22,
  output out_23,
  output out_24
);

  or or_1 (out_17, A0, B0);
  or or_2 (out_18, A1, B1);
  or or_3 (out_19, A2, B2);
  or or_4 (out_20, A3, B3);
  or or_5 (out_21, A4, B4);
  or or_6 (out_22, A5, B5);
  or or_7 (out_23, A6, B6);
  or or_8 (out_24, A7, B7);
endmodule

module NOT (
  input  A0,
  input  A1,
  input  A2,
  input  A3,
  input  A4,
  input  A5,
  input  A6,
  input  A7,
  output C0,
  output C1,
  output C2,
  output C3,
  output C4,
  output C5,
  output C6,
  output C7
);

  not not_1 (C0, A0);
  not not_2 (C1, A1);
  not not_3 (C2, A2);
  not not_4 (C3, A3);
  not not_5 (C4, A4);
  not not_6 (C5, A5);
  not not_7 (C6, A6);
  not not_8 (C7, A7);
endmodule

module CLA (
  input  P0,
  input  C0,
  input  G0,
  input  P1,
  input  G1,
  input  P2,
  input  G2,
  input  P3,
  input  G3,
  output C1,
  output C2,
  output C3,
  output C4
);

  wire and_1_out, and_2_out, and_3_out, and_4_out;

  and and_1 (and_1_out, P3, C3);
  or or_1 (C4, and_1_out, G3);
  and and_2 (and_2_out, P2, C2);
  or or_2 (C3, and_2_out, G2);
  and and_3 (and_3_out, P1, C1);
  or or_3 (C2, and_3_out, G1);
  and and_4 (and_4_out, P0, C0);
  or or_4 (C1, and_4_out, G0);
endmodule

module PFA (
  input  A,
  input  B,
  input  C1,
  output S,
  output P1,
  output G1
);

  wire xor_1_out;

  xor xor_1 (xor_1_out, A, B);
  xor xor_2 (S, xor_1_out, C1);
  or or_1 (P1, A, B);
  and and_1 (G1, A, B);
endmodule

module Add_Sub (
  input  A7,
  input  A6,
  input  A5,
  input  A4,
  input  A3,
  input  A2,
  input  A1,
  input  A0,
  input  B7,
  input  B6,
  input  B5,
  input  B4,
  input  B3,
  input  B2,
  input  B1,
  input  B0,
  input  D,
  input  Cin,
  output S7,
  output S6,
  output S5,
  output S4,
  output S3,
  output S2,
  output S1,
  output S0,
  output C8
);

  wire cla_1_c1, cla_1_c2, cla_1_c3, cla_2_c1, cla_2_c2, cla_2_c3, cla_2_c4, multiplexer_1_out,
       multiplexer_2_out, multiplexer_3_out, multiplexer_4_out, multiplexer_5_out, multiplexer_6_out,
       multiplexer_7_out, multiplexer_8_out, not_1_out, not_2_out, not_3_out, not_4_out, not_5_out,
       not_6_out, not_7_out, not_8_out, or_1_out, or_2_out, pfa_1_g1, pfa_1_p1, pfa_2_g1, pfa_2_p1, pfa_3_g1,
       pfa_3_p1, pfa_4_g1, pfa_4_p1, pfa_5_g1, pfa_5_p1, pfa_6_g1, pfa_6_p1, pfa_7_g1, pfa_7_p1, pfa_8_g1,
       pfa_8_p1;

  not not_1 (not_1_out, A7);
  Multiplexer #(.enable("false")) multiplexer_1 (.in0(A7), .in1(not_1_out), .out(multiplexer_1_out), .sel(D));
  PFA pfa_1 (.A(multiplexer_1_out), .B(B7), .C1(cla_1_c3), .S(S7), .P1(pfa_1_p1), .G1(pfa_1_g1));
  CLA cla_1 (
    .P3(pfa_1_p1), .G3(pfa_1_g1), .P2(pfa_2_p1), .G2(pfa_2_g1), .P1(pfa_3_p1), .G1(pfa_3_g1), .P0(pfa_4_p1),
    .C0(cla_2_c4), .G0(pfa_4_g1), .C4(C8), .C3(cla_1_c3), .C2(cla_1_c2), .C1(cla_1_c1));
  not not_2 (not_2_out, A6);
  Multiplexer #(.enable("false")) multiplexer_2 (.in0(A6), .in1(not_2_out), .out(multiplexer_2_out), .sel(D));
  PFA pfa_2 (.A(multiplexer_2_out), .B(B6), .C1(cla_1_c2), .S(S6), .P1(pfa_2_p1), .G1(pfa_2_g1));
  Multiplexer #(.enable("false")) multiplexer_3 (.in0(A5), .in1(not_3_out), .out(multiplexer_3_out), .sel(D));
  not not_3 (not_3_out, A5);
  PFA pfa_3 (.A(multiplexer_3_out), .B(B5), .C1(cla_1_c1), .S(S5), .P1(pfa_3_p1), .G1(pfa_3_g1));
  not not_4 (not_4_out, A4);
  Multiplexer #(.enable("false")) multiplexer_4 (.in0(A4), .in1(not_4_out), .out(multiplexer_4_out), .sel(D));
  PFA pfa_4 (.A(multiplexer_4_out), .B(B4), .C1(cla_2_c4), .S(S4), .P1(pfa_4_p1), .G1(pfa_4_g1));
  not not_5 (not_5_out, A3);
  Multiplexer #(.enable("false")) multiplexer_5 (.in0(A3), .in1(not_5_out), .out(multiplexer_5_out), .sel(D));
  PFA pfa_5 (.A(multiplexer_5_out), .B(B3), .C1(cla_2_c3), .S(S3), .P1(pfa_5_p1), .G1(pfa_5_g1));
  CLA cla_2 (
    .P3(pfa_5_p1), .G3(pfa_5_g1), .P2(pfa_6_p1), .G2(pfa_6_g1), .P1(pfa_7_p1), .G1(pfa_7_g1), .P0(pfa_8_p1),
    .C0(or_2_out), .G0(pfa_8_g1), .C4(cla_2_c4), .C3(cla_2_c3), .C2(cla_2_c2), .C1(cla_2_c1));
  not not_6 (not_6_out, A2);
  Multiplexer #(.enable("false")) multiplexer_6 (.in0(A2), .in1(not_6_out), .out(multiplexer_6_out), .sel(D));
  PFA pfa_6 (.A(multiplexer_6_out), .B(B2), .C1(cla_2_c2), .S(S2), .P1(pfa_6_p1), .G1(pfa_6_g1));
  not not_7 (not_7_out, A1);
  Multiplexer #(.enable("false")) multiplexer_7 (.in0(A1), .in1(not_7_out), .out(multiplexer_7_out), .sel(D));
  PFA pfa_7 (.A(multiplexer_7_out), .B(B1), .C1(cla_2_c1), .S(S1), .P1(pfa_7_p1), .G1(pfa_7_g1));
  not not_8 (not_8_out, A0);
  Multiplexer #(.enable("false")) multiplexer_8 (.in0(A0), .in1(not_8_out), .out(multiplexer_8_out), .sel(D));
  PFA pfa_8 (.A(multiplexer_8_out), .B(B0), .C1(or_1_out), .S(S0), .P1(pfa_8_p1), .G1(pfa_8_g1));
  or or_1 (or_1_out, Cin, D);
  or or_2 (or_2_out, Cin, D);
endmodule

module Immediate (
  input  [3:0] Opcode,
  input  [3:0] Bmux,
  output [3:0] Output_BMux
);

  wire addi_out, movi_out, or_1_out, subi_out;
  wire [3:0] and_1_out, bit_extender_1_out;

  and addi (addi_out, Opcode[3], ~Opcode[2], ~Opcode[1], ~Opcode[0]);  // AND_Gate
  and subi (subi_out, Opcode[3], ~Opcode[2], ~Opcode[1], Opcode[0]);  // AND_Gate
  or or_1 (or_1_out, addi_out, subi_out, movi_out);
  assign bit_extender_1_out = {{3{or_1_out}}, or_1_out};  // Bit_Extender bit_extender_1
  and movi (movi_out, Opcode[3], ~Opcode[2], Opcode[1], ~Opcode[0]);  // AND_Gate
  assign and_1_out = 4'b1001 & bit_extender_1_out;  // AND_Gate and_1, 4 bits wide
  assign Output_BMux = Bmux | and_1_out;  // OR_Gate or_2, 4 bits wide
endmodule

module PC_Counter (
  input  in_1,
  input  [3:0] in_2,
  output [4:0] out_3
);

  wire and_1_out, and_2_out, and_3_out, and_4_out, and_5_out, not_1_out, not_2_out;

  and and_1 (and_1_out, in_2[0], in_2[1], in_2[2], in_2[3]);
  not not_1 (not_1_out, in_1);
  and and_2 (and_2_out, not_1_out, not_2_out);
  not not_2 (not_2_out, and_1_out);
  J_K_Flip_Flop j_k_ff_1 (.J(1'b1), .clk(and_2_out), .K(1'b1), .Q(out_3[0]));  // open: Qn, preset, en, reset
  J_K_Flip_Flop j_k_ff_2 (.J(out_3[0]), .clk(and_2_out), .K(out_3[0]), .Q(out_3[1]));  // open: Qn, preset, en, reset
  and and_3 (and_3_out, out_3[0], out_3[1]);
  J_K_Flip_Flop j_k_ff_3 (.J(and_3_out), .clk(and_2_out), .K(and_3_out), .Q(out_3[2]));  // open: Qn, preset, en, reset
  and and_4 (and_4_out, and_3_out, out_3[2]);
  J_K_Flip_Flop j_k_ff_4 (.J(and_4_out), .clk(and_2_out), .K(and_4_out), .Q(out_3[3]));  // open: Qn, preset, en, reset
  and and_5 (and_5_out, and_4_out, out_3[3]);
  J_K_Flip_Flop j_k_ff_5 (.J(and_5_out), .clk(and_2_out), .K(and_5_out), .Q(out_3[4]));  // open: Qn, preset, en, reset
  // AND_Gate and_6 has open pins: in1=and_5_out, in4=out_3[4], out=open

  // Other names for the same wires on the sheet: A = out_3[0]; B = out_3[1]; C = out_3[2]; D = out_3[3]; E = out_3[4]
endmodule
