// Logisim project defualtABC.circ as structural Verilog: 2 circuits, main circuit main
module main (
  input  in_1,
  input  in_2,
  input  in_3,
  input  in_4,
  input  in_5,
  input  in_6,
  input  in_7,
  input  in_8,
  input  in_9,
  input  in_10,
  output out_11,
  output out_12,
  output out_13,
  output out_14,
  output out_15
);

  subtractor subtractor_1 (
    .D(in_9), .Cin(in_10), .A3(in_1), .B3(in_5), .A2(in_2), .B2(in_6), .A1(in_3), .B1(in_7), .A0(in_4),
    .B0(in_8), .S3(out_15), .S2(out_14), .S1(out_13), .S0(out_12), .out_15(out_11));
endmodule

module subtractor (
  input  A3,
  input  A2,
  input  A1,
  input  A0,
  input  B3,
  input  B2,
  input  B1,
  input  B0,
  input  D,
  input  Cin,
  output S3,
  output S2,
  output S1,
  output S0,
  output out_15
);

  wire multiplexer_1_out, multiplexer_2_out, multiplexer_3_out, multiplexer_4_out, not_1_out, not_2_out,
       not_3_out, not_4_out, pfa_1_p4, pfa_1_p5, pfa_1_p6, pfa_2_p3, pfa_2_p6, pfa_2_p7, pfa_3_p4, pfa_3_p7,
       pfa_3_p8, pfa_4_p5, pfa_4_p7, pfa_4_p8, pfa_4_p10;

  not not_1 (not_1_out, A3);
  Multiplexer #(.enable("false")) multiplexer_1 (.in0(A3), .in1(not_1_out), .out(multiplexer_1_out), .sel(D));
  // PFA pfa_1: pin names not known; wires that end beside it: multiplexer_1_out, S3, B3, pfa_1_p4, pfa_1_p5, pfa_1_p6
  // Carry_Look_Ahead carry_look_ahead_1: pin names not known; wires that end beside it: out_15, pfa_1_p4, pfa_1_p6, pfa_1_p5
  not not_2 (not_2_out, A2);
  Multiplexer #(.enable("false")) multiplexer_2 (.in0(A2), .in1(not_2_out), .out(multiplexer_2_out), .sel(D));
  // PFA pfa_2: pin names not known; wires that end beside it: multiplexer_2_out, S2, pfa_2_p3, B2, pfa_2_p3, pfa_2_p6, pfa_2_p7, pfa_2_p6
  not not_3 (not_3_out, A1);
  Multiplexer #(.enable("false")) multiplexer_3 (.in0(A1), .in1(not_3_out), .out(multiplexer_3_out), .sel(D));
  // PFA pfa_3: pin names not known; wires that end beside it: multiplexer_3_out, S1, pfa_2_p7, pfa_3_p4, B1, pfa_3_p4, pfa_3_p7, pfa_3_p8, pfa_3_p7
  not not_4 (not_4_out, A0);
  Multiplexer #(.enable("false")) multiplexer_4 (.in0(A0), .in1(not_4_out), .out(multiplexer_4_out), .sel(D));
  // PFA pfa_4: pin names not known; wires that end beside it: multiplexer_4_out, S0, pfa_3_p8, B0, pfa_4_p5, pfa_4_p5, pfa_4_p7, pfa_4_p8, pfa_4_p8, pfa_4_p10
  buf or_1 (pfa_4_p7, Cin);  // OR_Gate
  or or_2 (pfa_4_p10, Cin, D);
endmodule
