// Logisim project subtraction.circ as structural Verilog: 3 circuits, main circuit main
module subtraction (
  input  A7,
  input  A6,
  input  A5,
  input  A4,
  input  A3,
  input  A2,
  input  A1,
  input  A0,
  input  B7,
  input  B6,
  input  B5,
  input  B4,
  input  B3,
  input  B2,
  input  B1,
  input  B0,
  input  D,
  input  Cin,
  output S7,
  output S6,
  output S5,
  output S4,
  output S3,
  output S2,
  output S1,
  output S0,
  output C8
);

  wire carry_look_ahead_1_p2, carry_look_ahead_1_p3, carry_look_ahead_1_p4, carry_look_ahead_2_p5,
       carry_look_ahead_2_p6, carry_look_ahead_2_p7, multiplexer_1_out, multiplexer_2_out, multiplexer_3_out,
       multiplexer_4_out, multiplexer_5_out, multiplexer_6_out, multiplexer_7_out, multiplexer_8_out,
       not_1_out, not_2_out, not_3_out, not_4_out, not_5_out, not_6_out, not_7_out, not_8_out, pfa_2_p3,
       pfa_2_p6, pfa_2_p7, pfa_3_p4, pfa_3_p7, pfa_3_p8, pfa_4_p5, pfa_4_p6, pfa_4_p7, pfa_6_p3, pfa_6_p6,
       pfa_6_p7, pfa_7_p4, pfa_7_p7, pfa_7_p8, pfa_8_p5, pfa_8_p7, pfa_8_p8, pfa_8_p10;

  // Carry_Look_Ahead carry_look_ahead_1: pin names not known; wires that end beside it: C8, carry_look_ahead_1_p2, carry_look_ahead_1_p3, carry_look_ahead_1_p4
  not not_1 (not_1_out, A7);
  Multiplexer #(.enable("false")) multiplexer_1 (.in0(A7), .in1(not_1_out), .out(multiplexer_1_out), .sel(D));
  // PFA pfa_1: pin names not known; wires that end beside it: multiplexer_1_out, S7, B7, carry_look_ahead_1_p2, carry_look_ahead_1_p4, carry_look_ahead_1_p3
  not not_2 (not_2_out, A6);
  Multiplexer #(.enable("false")) multiplexer_2 (.in0(A6), .in1(not_2_out), .out(multiplexer_2_out), .sel(D));
  // PFA pfa_2: pin names not known; wires that end beside it: multiplexer_2_out, S6, pfa_2_p3, B6, pfa_2_p3, pfa_2_p6, pfa_2_p7, pfa_2_p6
  Multiplexer #(.enable("false")) multiplexer_3 (.in0(A5), .in1(not_3_out), .out(multiplexer_3_out), .sel(D));
  not not_3 (not_3_out, A5);
  // PFA pfa_3: pin names not known; wires that end beside it: multiplexer_3_out, S5, pfa_2_p7, pfa_3_p4, B5, pfa_3_p4, pfa_3_p7, pfa_3_p8, pfa_3_p7
  not not_4 (not_4_out, A4);
  Multiplexer #(.enable("false")) multiplexer_4 (.in0(A4), .in1(not_4_out), .out(multiplexer_4_out), .sel(D));
  // PFA pfa_4: pin names not known; wires that end beside it: multiplexer_4_out, S4, pfa_3_p8, B4, pfa_4_p5, pfa_4_p6, pfa_4_p7
  // Carry_Look_Ahead carry_look_ahead_2: pin names not known; wires that end beside it: pfa_4_p5, pfa_4_p7, pfa_4_p6, pfa_4_p6, carry_look_ahead_2_p5, carry_look_ahead_2_p6, carry_look_ahead_2_p7
  not not_5 (not_5_out, A3);
  Multiplexer #(.enable("false")) multiplexer_5 (.in0(A3), .in1(not_5_out), .out(multiplexer_5_out), .sel(D));
  // PFA pfa_5: pin names not known; wires that end beside it: multiplexer_5_out, S3, B3, carry_look_ahead_2_p5, carry_look_ahead_2_p7, carry_look_ahead_2_p6
  not not_6 (not_6_out, A2);
  Multiplexer #(.enable("false")) multiplexer_6 (.in0(A2), .in1(not_6_out), .out(multiplexer_6_out), .sel(D));
  // PFA pfa_6: pin names not known; wires that end beside it: multiplexer_6_out, S2, pfa_6_p3, B2, pfa_6_p3, pfa_6_p6, pfa_6_p7, pfa_6_p6
  not not_7 (not_7_out, A1);
  Multiplexer #(.enable("false")) multiplexer_7 (.in0(A1), .in1(not_7_out), .out(multiplexer_7_out), .sel(D));
  // PFA pfa_7: pin names not known; wires that end beside it: multiplexer_7_out, S1, pfa_6_p7, pfa_7_p4, B1, pfa_7_p4, pfa_7_p7, pfa_7_p8, pfa_7_p7
  not not_8 (not_8_out, A0);
  Multiplexer #(.enable("false")) multiplexer_8 (.in0(A0), .in1(not_8_out), .out(multiplexer_8_out), .sel(D));
  // PFA pfa_8: pin names not known; wires that end beside it: multiplexer_8_out, S0, pfa_7_p8, B0, pfa_8_p5, pfa_8_p5, pfa_8_p7, pfa_8_p8, pfa_8_p8, pfa_8_p10
  or or_1 (pfa_8_p7, Cin, D);
  or or_2 (pfa_8_p10, Cin, D);
endmodule

module main (
  input  in_1,
  input  in_2,
  input  in_3,
  input  in_4,
  input  in_5,
  input  in_6,
  input  in_7,
  input  in_8,
  input  in_9,
  input  in_10,
  input  in_11,
  input  in_12,
  input  in_13,
  input  in_14,
  input  in_15,
  input  in_16,
  input  in_17,
  input  in_18,
  output out_19,
  output out_20,
  output out_21,
  output out_22,
  output out_23,
  output out_24,
  output out_25,
  output out_26,
  output out_27
);

  subtraction subtraction_1 (
    .D(in_17), .C8(out_19), .S3(out_23), .S2(out_22), .S1(out_21), .S0(out_20), .S7(out_27), .S6(out_26),
    .S5(out_25), .S4(out_24), .Cin(in_18), .A5(in_6), .B5(in_5), .A7(in_2), .A6(in_4), .B7(in_1), .B6(in_3),
    .A0(in_16), .B0(in_15), .A3(in_10), .A2(in_12), .B3(in_9), .B2(in_11), .A1(in_14), .B1(in_13), .A4(in_8),
    .B4(in_7));
endmodule

module _1bitFullAdd (
  input  A,
  input  B,
  input  Cin,
  output S,
  output Cout
);

  wire and_1_out, and_2_out, xor_1_out;

  xor xor_1 (xor_1_out, A, B);
  xor xor_2 (S, xor_1_out, Cin);
  and and_1 (and_1_out, xor_1_out, Cin);
  and and_2 (and_2_out, A, B);
  or or_1 (Cout, and_1_out, and_2_out);
endmodule
